// Logisim project code_decode_seg.circ as structural Verilog: 33 circuits, main circuit main
module main (
  input  I0,
  input  I1,
  input  I2,
  input  I3,
  input  I4,
  input  I5,
  input  I6,
  input  I7,
  input  I8,
  input  I9,
  input  I10,
  input  I11,
  input  in_13,
  input  I12,
  input  I13,
  input  I14,
  input  I15,
  input  I0_2,
  input  I1_2,
  input  I2_2,
  input  in_21,
  input  I3_2,
  input  I4_2,
  input  I5_2,
  input  I6_2,
  input  I7_2,
  input  I8_2,
  input  I9_2,
  input  I10_2,
  input  I11_2,
  input  I12_2,
  input  I13_2,
  input  I14_2,
  input  I15_2
);

  wire control_8_1_y0, control_8_1_y1, control_8_1_y2, control_8_1_y3, control_8_1_y4, control_8_1_y5,
       controler_1_out_6, controler_1_out_7, controler_1_out_8, controler_1_out_9, controlled_buffer_1_out,
       counter_3_1_out_2, counter_3_1_out_3, counter_3_1_out_4, decode_1_y0, decode_1_y1, decode_1_y2,
       decode_1_y3, decode_1_y4, decode_1_y5, decode_1_y6, decode_1_y7, n2_seg_1_out_6, n2_seg_1_out_7,
       n2_seg_1_out_8, n2_seg_1_out_9, n2_seg_1_out_10, n2_seg_1_out_11, n2_seg_1_out_12, n2_seg_1_out_13,
       n2_seg_1_out_14, n2_seg_1_out_15, n2_seg_1_out_16, n2_seg_1_out_17, n2_seg_1_out_18, n2_seg_1_out_19,
       n4_add_sub_1_cn_1, n4_add_sub_1_s0, n4_add_sub_1_s1, n4_add_sub_1_s2, n4_add_sub_1_s3, n16_4_1_z0,
       n16_4_1_z1, n16_4_1_z2, n16_4_1_z3, n16_4_2_z0, n16_4_2_z1, n16_4_2_z2, n16_4_2_z3, not_1_out,
       regisiter5_1_out_7, regisiter5_1_out_8, regisiter5_1_out_9, regisiter5_1_out_10, regisiter5_1_out_11,
       regisiter_1_out_6, regisiter_1_out_7, regisiter_1_out_8, regisiter_1_out_9, regisiter_2_out_6,
       regisiter_2_out_7, regisiter_2_out_8, regisiter_2_out_9;

  _16_4 u_16_4_1 (
    .A0(I0), .A1(I1), .A2(I2), .A3(I3), .A4(I4), .A5(I5), .A6(I6), .A7(I7), .A8(I8), .A9(I9), .A10(I10),
    .A11(I11), .A12(I12), .A13(I13), .A14(I14), .A15(I15), .Z0(n16_4_1_z0), .Z1(n16_4_1_z1), .Z2(n16_4_1_z2),
    .Z3(n16_4_1_z3));  // open: out_21
  _16_4 u_16_4_2 (
    .A0(I0_2), .A1(I1_2), .A2(I2_2), .A3(I3_2), .A4(I4_2), .A5(I5_2), .A6(I6_2), .A7(I7_2), .A8(I8_2),
    .A9(I9_2), .A10(I10_2), .A11(I11_2), .A12(I12_2), .A13(I13_2), .A14(I14_2), .A15(I15_2), .Z0(n16_4_2_z0),
    .Z1(n16_4_2_z1), .Z2(n16_4_2_z2), .Z3(n16_4_2_z3));  // open: out_21
  controler controler_1 (
    .in_2(n16_4_1_z0), .in_3(n16_4_1_z1), .in_4(n16_4_1_z2), .in_5(n16_4_1_z3), .in_1(control_8_1_y0),
    .out_6(controler_1_out_6), .out_7(controler_1_out_7), .out_8(controler_1_out_8), .out_9(controler_1_out_9));
  controler controler_2 (
    .in_2(n16_4_2_z0), .in_3(n16_4_2_z1), .in_4(n16_4_2_z2), .in_5(n16_4_2_z3), .in_1(control_8_1_y2),
    .out_6(controler_1_out_6), .out_7(controler_1_out_7), .out_8(controler_1_out_8), .out_9(controler_1_out_9));
  LED led_1 (.in(controler_1_out_6));
  LED led_2 (.in(controler_1_out_8));
  LED led_3 (.in(controler_1_out_7));
  LED led_4 (.in(controler_1_out_9));
  assign controlled_buffer_1_out = not_1_out ? 1'b0 : 1'bz;  // Controlled_Buffer controlled_buffer_1
  not not_1 (not_1_out, control_8_1_y5);
  regisiter regisiter_1 (
    .in_1(controler_1_out_9), .in_2(controler_1_out_8), .in_3(controler_1_out_7), .in_4(controler_1_out_6),
    .in_5(control_8_1_y1), .out_6(regisiter_1_out_6), .out_7(regisiter_1_out_7), .out_8(regisiter_1_out_8),
    .out_9(regisiter_1_out_9));
  regisiter regisiter_2 (
    .in_1(controler_1_out_9), .in_2(controler_1_out_8), .in_3(controler_1_out_7), .in_4(controler_1_out_6),
    .in_5(control_8_1_y3), .out_6(regisiter_2_out_6), .out_7(regisiter_2_out_7), .out_8(regisiter_2_out_8),
    .out_9(regisiter_2_out_9));
  _2_seg u_2_seg_1 (
    .in_1(controlled_buffer_1_out), .in_2(controler_1_out_9), .in_3(controler_1_out_8),
    .in_4(controler_1_out_7), .in_5(controler_1_out_6), .out_6(n2_seg_1_out_6), .out_7(n2_seg_1_out_7),
    .out_8(n2_seg_1_out_8), .out_9(n2_seg_1_out_9), .out_10(n2_seg_1_out_10), .out_11(n2_seg_1_out_11),
    .out_12(n2_seg_1_out_12), .out_13(n2_seg_1_out_13), .out_14(n2_seg_1_out_14), .out_15(n2_seg_1_out_15),
    .out_16(n2_seg_1_out_16), .out_17(n2_seg_1_out_17), .out_18(n2_seg_1_out_18), .out_19(n2_seg_1_out_19));
  _4_add_sub u_4_add_sub_1 (
    .A3(regisiter_1_out_6), .A2(regisiter_1_out_7), .A1(regisiter_1_out_8), .A0(regisiter_1_out_9),
    .B3(regisiter_2_out_6), .B2(regisiter_2_out_7), .B1(regisiter_2_out_8), .B0(regisiter_2_out_9),
    .Cn_1(n4_add_sub_1_cn_1), .S3(n4_add_sub_1_s3), .S2(n4_add_sub_1_s2), .S1(n4_add_sub_1_s1),
    .S0(n4_add_sub_1_s0), .S(in_21));
  _7_Segment_Display u_7_segment_display_1 (
    .g(n2_seg_1_out_12), .f(n2_seg_1_out_11), .a(n2_seg_1_out_6), .b(n2_seg_1_out_7), .e(n2_seg_1_out_10),
    .d(n2_seg_1_out_9), .c(n2_seg_1_out_8), .dp(1'b0));
  regisiter5 regisiter5_1 (
    .in_1(n4_add_sub_1_cn_1), .in_2(n4_add_sub_1_s3), .in_3(n4_add_sub_1_s2), .in_4(n4_add_sub_1_s1),
    .in_5(n4_add_sub_1_s0), .in_6(control_8_1_y4), .out_7(regisiter5_1_out_7), .out_8(regisiter5_1_out_8),
    .out_9(regisiter5_1_out_9), .out_10(regisiter5_1_out_10), .out_11(regisiter5_1_out_11));
  controler5 controler5_1 (
    .in_2(regisiter5_1_out_7), .in_3(regisiter5_1_out_8), .in_4(regisiter5_1_out_9),
    .in_5(regisiter5_1_out_10), .in_6(regisiter5_1_out_11), .in_1(control_8_1_y5),
    .out_7(controlled_buffer_1_out), .out_8(controler_1_out_9), .out_9(controler_1_out_8),
    .out_10(controler_1_out_7), .out_11(controler_1_out_6));
  _7_Segment_Display u_7_segment_display_2 (
    .g(n2_seg_1_out_19), .f(n2_seg_1_out_18), .a(n2_seg_1_out_13), .b(n2_seg_1_out_14), .e(n2_seg_1_out_17),
    .d(n2_seg_1_out_16), .c(n2_seg_1_out_15), .dp(1'b0));
  counter_3 counter_3_1 (.out_2(counter_3_1_out_2), .out_3(counter_3_1_out_3), .out_4(counter_3_1_out_4), .in_1(in_13));
  decode decode_1 (
    .A0(counter_3_1_out_2), .A1(counter_3_1_out_3), .A2(counter_3_1_out_4), .Y0(decode_1_y0),
    .Y1(decode_1_y1), .Y2(decode_1_y2), .Y3(decode_1_y3), .Y4(decode_1_y4), .Y5(decode_1_y5),
    .Y6(decode_1_y6), .Y7(decode_1_y7));
  control_8 control_8_1 (
    .I7(decode_1_y7), .I6(decode_1_y6), .I5(decode_1_y5), .I3(decode_1_y3), .I2(decode_1_y2),
    .I1(decode_1_y1), .I0(decode_1_y0), .Y5(control_8_1_y5), .Y4(control_8_1_y4), .Y3(control_8_1_y3),
    .Y2(control_8_1_y2), .Y1(control_8_1_y1), .Y0(control_8_1_y0));
  LED led_5 (.in(decode_1_y0));
  LED led_6 (.in(decode_1_y1));
  LED led_7 (.in(decode_1_y2));
  LED led_8 (.in(decode_1_y3));
  LED led_9 (.in(decode_1_y4));
  LED led_10 (.in(decode_1_y5));
  LED led_11 (.in(decode_1_y6));
  LED led_12 (.in(decode_1_y7));
endmodule

module code (
  input  I0,
  input  I1,
  input  I2,
  input  I3,
  input  I4,
  input  I5,
  input  I6,
  input  I7,
  output Y0,
  output Y1,
  output Y2
);

  or or_1 (Y0, I1, I3, I5, I7);
  or or_2 (Y1, I2, I3, I6, I7);
  or or_3 (Y2, I4, I5, I6, I7);
endmodule

module decode (
  input  A0,
  input  A1,
  input  A2,
  output Y0,
  output Y1,
  output Y2,
  output Y3,
  output Y4,
  output Y5,
  output Y6,
  output Y7
);

  wire not_1_out, not_2_out, not_3_out;

  not not_1 (not_1_out, A0);
  not not_2 (not_2_out, A1);
  not not_3 (not_3_out, A2);
  and and_1 (Y0, not_1_out, not_3_out, not_2_out);
  and and_2 (Y1, A0, not_2_out, not_3_out);
  and and_3 (Y2, not_1_out, A1, not_3_out);
  and and_4 (Y3, not_3_out, A1, A0);
  and and_5 (Y4, not_1_out, not_2_out, A2);
  and and_6 (Y5, A0, not_2_out, A2);
  and and_7 (Y6, not_1_out, A1, A2);
  and and_8 (Y7, A0, A1, A2);
endmodule

module a (
  input  A,
  input  B,
  input  C,
  input  D,
  output a_2
);

  wire and_1_out, and_2_out, not_1_out, not_2_out;

  not not_1 (not_1_out, B);
  not not_2 (not_2_out, D);
  and and_1 (and_1_out, not_1_out, not_2_out);
  and and_2 (and_2_out, B, D);
  or or_1 (a_2, A, and_1_out, C, and_2_out);
endmodule

module b (
  input  A,
  input  B,
  input  C,
  input  D,
  output b_2
);

  wire and_1_out, and_2_out, not_1_out, not_2_out, not_3_out;

  not not_1 (not_1_out, C);
  not not_2 (not_2_out, D);
  not not_3 (not_3_out, B);
  and and_1 (and_1_out, not_1_out, not_2_out);
  and and_2 (and_2_out, C, D);
  or or_1 (b_2, not_3_out, and_1_out, and_2_out);
endmodule

module c (
  input  A,
  input  B,
  input  C,
  input  D,
  output c_2
);

  wire not_1_out;

  not not_1 (not_1_out, C);
  or or_1 (c_2, B, not_1_out, D);
endmodule

module d (
  input  A,
  input  B,
  input  C,
  input  D,
  output d_2
);

  wire and_1_out, and_2_out, and_3_out, and_4_out, not_1_out, not_2_out, not_3_out, not_4_out, not_5_out;

  not not_1 (not_1_out, B);
  not not_2 (not_2_out, D);
  not not_3 (not_3_out, B);
  not not_4 (not_4_out, D);
  not not_5 (not_5_out, C);
  and and_1 (and_1_out, not_1_out, not_2_out);
  and and_2 (and_2_out, not_3_out, C);
  and and_3 (and_3_out, C, not_4_out);
  and and_4 (and_4_out, B, not_5_out, D);
  or or_1 (d_2, and_1_out, and_2_out, A, and_3_out, and_4_out);
endmodule

module e (
  input  A,
  input  B,
  input  C,
  input  D,
  output e
);

  wire and_1_out, and_2_out, not_1_out, not_2_out;

  not not_1 (not_1_out, B);
  not not_2 (not_2_out, D);
  and and_1 (and_1_out, not_1_out, not_2_out);
  and and_2 (and_2_out, C, not_2_out);
  or or_1 (e, and_1_out, and_2_out);
endmodule

module f (
  input  A,
  input  B,
  input  C,
  input  D,
  output f
);

  wire and_1_out, and_2_out, and_3_out, not_1_out, not_2_out;

  not not_1 (not_1_out, C);
  not not_2 (not_2_out, D);
  and and_1 (and_1_out, B, not_1_out);
  and and_2 (and_2_out, B, not_2_out);
  and and_3 (and_3_out, not_1_out, not_2_out);
  or or_1 (f, and_1_out, A, and_2_out, and_3_out);
endmodule

module g (
  input  A,
  input  B,
  input  C,
  input  D,
  output g
);

  wire and_1_out, not_1_out, xor_1_out;

  not not_1 (not_1_out, D);
  xor xor_1 (xor_1_out, B, C);
  and and_1 (and_1_out, C, not_1_out);
  or or_1 (g, A, xor_1_out, and_1_out);
endmodule

module seg (
  input  A,
  input  B,
  input  C,
  input  D,
  output out_5,
  output out_6,
  output out_7,
  output out_8,
  output out_9,
  output out_10,
  output out_11
);

  a a_1 (.A(A), .B(B), .C(C), .D(D), .a_2(out_5));
  b b_1 (.A(A), .B(B), .C(C), .D(D), .b_2(out_6));
  c c_1 (.A(A), .B(B), .C(C), .D(D), .c_2(out_7));
  d d_1 (.A(A), .B(B), .C(C), .D(D), .d_2(out_8));
  e e_1 (.A(A), .B(B), .C(C), .D(D), .e(out_9));
  f f_1 (.A(A), .B(B), .C(C), .D(D), .f(out_10));
  g g_1 (.A(A), .B(B), .C(C), .D(D), .g(out_11));
endmodule

module _8_3code_prior (
  input  I0_prime,
  input  I1_prime,
  input  I2_prime,
  input  I3_prime,
  input  I4_prime,
  input  I5_prime,
  input  I6_prime,
  input  I7_prime,
  input  S_prime,
  output Ys_prime,
  output Yex_prime,
  output Y0_prime,
  output Y1_prime,
  output Y2_prime
);

  wire and_1_out, and_2_out, and_3_out, and_4_out, and_5_out, and_6_out, and_7_out, and_8_out, and_9_out,
       and_10_out, and_11_out, and_12_out, not_1_out, not_2_out, not_3_out, not_4_out, not_5_out, not_6_out,
       not_7_out, not_8_out, not_9_out, not_10_out, not_11_out, not_12_out;

  not not_1 (not_1_out, I1_prime);
  not not_2 (not_2_out, I2_prime);
  not not_3 (not_3_out, I3_prime);
  not not_4 (not_4_out, I4_prime);
  not not_5 (not_5_out, I5_prime);
  not not_6 (not_6_out, I6_prime);
  not not_7 (not_7_out, I7_prime);
  not not_8 (not_8_out, S_prime);
  not not_9 (not_9_out, not_2_out);
  not not_10 (not_10_out, not_4_out);
  not not_11 (not_11_out, not_5_out);
  not not_12 (not_12_out, not_6_out);
  and and_1 (and_1_out, not_1_out, not_9_out, not_10_out, not_12_out, not_8_out);
  and and_2 (and_2_out, not_3_out, not_10_out, not_12_out, not_8_out);
  and and_3 (and_3_out, not_5_out, not_12_out, not_8_out);
  and and_4 (and_4_out, not_7_out, not_8_out);
  and and_5 (and_5_out, not_2_out, not_10_out, not_11_out, not_8_out);
  and and_6 (and_6_out, not_3_out, not_10_out, not_11_out, not_8_out);
  and and_7 (and_7_out, not_6_out, not_8_out);
  and and_8 (and_8_out, not_7_out, not_8_out);
  and and_9 (and_9_out, not_4_out, not_8_out);
  and and_10 (and_10_out, not_5_out, not_8_out);
  and and_11 (and_11_out, not_6_out, not_8_out);
  and and_12 (and_12_out, not_7_out, not_8_out);
  nand nand_1 (Ys_prime, I0_prime, I1_prime, I2_prime, I3_prime, I4_prime, I5_prime, I6_prime, I7_prime, not_8_out);
  nand nand_2 (Yex_prime, Ys_prime, not_8_out);
  nor nor_1 (Y0_prime, and_1_out, and_2_out, and_3_out, and_4_out);
  nor nor_2 (Y1_prime, and_5_out, and_6_out, and_7_out, and_8_out);
  nor nor_3 (Y2_prime, and_9_out, and_10_out, and_11_out, and_12_out);
endmodule

module _16_4 (
  input  A0,
  input  A1,
  input  A2,
  input  A3,
  input  A4,
  input  A5,
  input  A6,
  input  A7,
  input  A8,
  input  A9,
  input  A10,
  input  A11,
  input  A12,
  input  A13,
  input  A14,
  input  A15,
  output Z0,
  output Z1,
  output Z2,
  output Z3,
  output out_21
);

  wire n8_3code_prior_1_y0_prime, n8_3code_prior_1_y1_prime, n8_3code_prior_1_y2_prime,
       n8_3code_prior_2_y0_prime, n8_3code_prior_2_y1_prime, n8_3code_prior_2_y2_prime,
       n8_3code_prior_2_yex_prime, not_1_out, not_2_out, not_3_out, not_4_out, not_5_out, not_6_out,
       not_7_out, not_8_out, not_9_out, not_10_out, not_11_out, not_12_out, not_13_out, not_14_out,
       not_15_out, not_16_out;

  not not_1 (not_1_out, A0);
  not not_2 (not_2_out, A1);
  not not_3 (not_3_out, A2);
  not not_4 (not_4_out, A3);
  not not_5 (not_5_out, A4);
  not not_6 (not_6_out, A5);
  not not_7 (not_7_out, A6);
  not not_8 (not_8_out, A7);
  not not_9 (not_9_out, A8);
  not not_10 (not_10_out, A9);
  not not_11 (not_11_out, A10);
  not not_12 (not_12_out, A11);
  not not_13 (not_13_out, A12);
  not not_14 (not_14_out, A13);
  not not_15 (not_15_out, A14);
  not not_16 (not_16_out, A15);
  _8_3code_prior u_8_3code_prior_1 (
    .I0_prime(not_1_out), .I1_prime(not_2_out), .I2_prime(not_3_out), .I3_prime(not_4_out),
    .I4_prime(not_5_out), .I5_prime(not_6_out), .I6_prime(not_7_out), .I7_prime(not_8_out), .S_prime(out_21),
    .Y0_prime(n8_3code_prior_1_y0_prime), .Y1_prime(n8_3code_prior_1_y1_prime),
    .Y2_prime(n8_3code_prior_1_y2_prime));  // open: Ys_prime, Yex_prime
  _8_3code_prior u_8_3code_prior_2 (
    .I0_prime(not_9_out), .I1_prime(not_10_out), .I2_prime(not_11_out), .I3_prime(not_12_out),
    .I4_prime(not_13_out), .I5_prime(not_14_out), .I6_prime(not_15_out), .I7_prime(not_16_out),
    .S_prime(1'b0), .Ys_prime(out_21), .Yex_prime(n8_3code_prior_2_yex_prime),
    .Y0_prime(n8_3code_prior_2_y0_prime), .Y1_prime(n8_3code_prior_2_y1_prime),
    .Y2_prime(n8_3code_prior_2_y2_prime));
  not not_17 (Z3, n8_3code_prior_2_yex_prime);
  nand nand_1 (Z0, n8_3code_prior_1_y0_prime, n8_3code_prior_2_y0_prime);
  nand nand_2 (Z1, n8_3code_prior_1_y1_prime, n8_3code_prior_2_y1_prime);
  nand nand_3 (Z2, n8_3code_prior_1_y2_prime, n8_3code_prior_2_y2_prime);
endmodule

module _2_10decode (
  input  A0,
  input  A1,
  input  A2,
  input  A3,
  output Y0,
  output Y1,
  output Y2,
  output Y3,
  output Y4,
  output Y5,
  output Y6,
  output Y7,
  output Y8,
  output Y9_prime
);

  wire not_1_out, not_2_out, not_3_out, not_4_out;

  not not_1 (not_1_out, A0);
  not not_2 (not_2_out, A1);
  not not_3 (not_3_out, A2);
  not not_4 (not_4_out, A3);
  and and_1 (Y0, not_1_out, not_2_out, not_3_out, not_4_out);
  and and_2 (Y1, A0, not_2_out, not_3_out, not_4_out);
  and and_3 (Y2, not_1_out, A1, not_3_out, not_4_out);
  and and_4 (Y3, A0, A1, not_3_out, not_4_out);
  and and_5 (Y4, not_1_out, not_2_out, A2, not_4_out);
  and and_6 (Y5, A0, not_2_out, A2, not_4_out);
  and and_7 (Y6, not_1_out, A1, A2, not_4_out);
  and and_8 (Y7, A0, A1, A2, not_4_out);
  and and_9 (Y8, not_1_out, not_2_out, not_3_out, A3);
  and and_10 (Y9_prime, A0, not_2_out, not_3_out, A3);
endmodule

module _4_16 (
  input  A0,
  input  A1,
  input  A2,
  input  A3,
  output Y0,
  output Y1,
  output Y2,
  output Y3,
  output Y4,
  output Y5,
  output Y6,
  output Y7,
  output Y8,
  output Y9,
  output Y10,
  output Y11,
  output Y12,
  output Y13,
  output Y14,
  output Y15
);

  wire not_1_out, not_2_out, not_3_out, not_4_out;

  not not_1 (not_1_out, A0);
  not not_2 (not_2_out, A1);
  not not_3 (not_3_out, A2);
  not not_4 (not_4_out, A3);
  and and_1 (Y0, not_1_out, not_2_out, not_3_out, not_4_out);
  and and_2 (Y1, A0, not_2_out, not_3_out, not_4_out);
  and and_3 (Y2, not_1_out, A1, not_3_out, not_4_out);
  and and_4 (Y3, A0, A1, not_3_out, not_4_out);
  and and_5 (Y4, not_1_out, not_2_out, A2, not_4_out);
  and and_6 (Y5, A0, not_2_out, A2, not_4_out);
  and and_7 (Y6, not_1_out, A1, A2, not_4_out);
  and and_8 (Y7, A0, A1, A2, not_4_out);
  and and_9 (Y8, not_1_out, not_2_out, not_3_out, A3);
  and and_10 (Y9, A0, not_2_out, not_3_out, A3);
  and and_11 (Y10, not_1_out, A1, not_3_out, A3);
  and and_12 (Y11, A0, A1, not_3_out, A3);
  and and_13 (Y12, not_1_out, not_2_out, A2, A3);
  and and_14 (Y13, A0, not_2_out, A2, A3);
  and and_15 (Y14, not_1_out, A1, A2, A3);
  and and_16 (Y15, A0, A1, A2, A3);
endmodule

module controler (
  input  in_1,
  input  in_2,
  input  in_3,
  input  in_4,
  input  in_5,
  output out_6,
  output out_7,
  output out_8,
  output out_9
);

  assign out_6 = in_1 ? in_2 : 1'bz;  // Controlled_Buffer controlled_buffer_1
  assign out_7 = in_1 ? in_3 : 1'bz;  // Controlled_Buffer controlled_buffer_2
  assign out_8 = in_1 ? in_4 : 1'bz;  // Controlled_Buffer controlled_buffer_3
  assign out_9 = in_1 ? in_5 : 1'bz;  // Controlled_Buffer controlled_buffer_4
endmodule

module regisiter (
  input  in_1,
  input  in_2,
  input  in_3,
  input  in_4,
  input  in_5,
  output out_6,
  output out_7,
  output out_8,
  output out_9
);

  D_Flip_Flop d_ff_1 (.clk(in_5), .D(in_1), .Q(out_6));  // open: Qn, preset, en, reset
  D_Flip_Flop d_ff_2 (.clk(in_5), .D(in_2), .Q(out_7));  // open: Qn, preset, en, reset
  D_Flip_Flop d_ff_3 (.clk(in_5), .D(in_3), .Q(out_8));  // open: Qn, preset, en, reset
  D_Flip_Flop d_ff_4 (.clk(in_5), .D(in_4), .Q(out_9));  // open: Qn, preset, en, reset
endmodule

module HA (
  input  Ai,
  input  Bi,
  output Si,
  output Ci_1
);

  xor xor_1 (Si, Ai, Bi);
  and and_1 (Ci_1, Ai, Bi);
endmodule

module FA (
  input  Cn_1,
  input  An,
  input  Bn,
  output Sn,
  output Cn
);

  wire ha_1_ci_1, ha_1_si, ha_2_ci_1;

  HA ha_1 (.Ai(An), .Bi(Bn), .Si(ha_1_si), .Ci_1(ha_1_ci_1));
  HA ha_2 (.Ai(Cn_1), .Bi(ha_1_si), .Si(Sn), .Ci_1(ha_2_ci_1));
  or or_1 (Cn, ha_2_ci_1, ha_1_ci_1);
endmodule

module _4_ADD (
  input  A3,
  input  A2,
  input  A1,
  input  A0,
  input  B3,
  input  B2,
  input  B1,
  input  B0,
  output Cn_1,
  output S3,
  output S2,
  output S1,
  output S0
);

  wire fa_1_cn, fa_2_cn, fa_3_cn;

  FA fa_1 (.Cn_1(1'b0), .An(A0), .Bn(B0), .Sn(S0), .Cn(fa_1_cn));
  FA fa_2 (.Cn_1(fa_1_cn), .An(A1), .Bn(B1), .Sn(S1), .Cn(fa_2_cn));
  FA fa_3 (.Cn_1(fa_2_cn), .An(A2), .Bn(B2), .Sn(S2), .Cn(fa_3_cn));
  FA fa_4 (.Cn_1(fa_3_cn), .An(A3), .Bn(B3), .Sn(S3), .Cn(Cn_1));
endmodule

module counter (
  input  in_1,
  output out_2,
  output out_3,
  output out_4,
  output out_5
);

  wire clock_1_out, not_1_out, not_2_out, not_3_out;

  Clock clock_1 (.out(clock_1_out));
  not not_1 (not_1_out, out_2);
  not not_2 (not_2_out, out_3);
  not not_3 (not_3_out, out_4);
  T_Flip_Flop t_ff_1 (.clk(clock_1_out), .T(in_1), .Q(out_2));  // open: Qn, preset, reset, en
  T_Flip_Flop t_ff_2 (.clk(not_1_out), .T(in_1), .Q(out_3));  // open: Qn, preset, reset, en
  T_Flip_Flop t_ff_3 (.clk(not_2_out), .T(in_1), .Q(out_4));  // open: Qn, preset, reset, en
  T_Flip_Flop t_ff_4 (.clk(not_3_out), .T(in_1), .Q(out_5));  // open: Qn, preset, reset, en
endmodule

module refer (
  input  A,
  input  B,
  input  C,
  input  D,
  output Y7,
  output Y6,
  output Y5,
  output Y4,
  output Y3,
  output Y2,
  output Y1,
  output Y0
);

  wire and_1_out, and_2_out, and_4_out, and_5_out, and_6_out, and_7_out, not_1_out, not_2_out, not_3_out;

  not not_1 (not_1_out, A);
  not not_2 (not_2_out, B);
  not not_3 (not_3_out, C);
  and and_1 (and_1_out, A, B);
  and and_2 (and_2_out, A, C);
  and and_3 (Y3, A, not_2_out, not_3_out);
  and and_4 (and_4_out, not_1_out, B);
  and and_5 (and_5_out, B, C);
  and and_6 (and_6_out, not_1_out, C);
  and and_7 (and_7_out, A, B, not_3_out);
  or or_1 (Y4, and_1_out, and_2_out);
  or or_2 (Y2, and_4_out, and_5_out);
  or or_3 (Y1, and_6_out, and_7_out);

  assign Y0 = D;
  assign Y5 = 1'b0;
  assign Y6 = 1'b0;
  assign Y7 = 1'b0;
endmodule

module _2_seg (
  input  in_1,
  input  in_2,
  input  in_3,
  input  in_4,
  input  in_5,
  output out_6,
  output out_7,
  output out_8,
  output out_9,
  output out_10,
  output out_11,
  output out_12,
  output out_13,
  output out_14,
  output out_15,
  output out_16,
  output out_17,
  output out_18,
  output out_19
);

  wire refer2_1_y0, refer2_1_y1, refer2_1_y2, refer2_1_y3, refer2_1_y4, refer2_1_y5, refer2_1_y6, refer2_1_y7;

  refer2 refer2_1 (
    .A(in_1), .B(in_2), .C(in_3), .D(in_4), .E(in_5), .Y7(refer2_1_y7), .Y6(refer2_1_y6), .Y5(refer2_1_y5),
    .Y4(refer2_1_y4), .Y3(refer2_1_y3), .Y2(refer2_1_y2), .Y1(refer2_1_y1), .Y0(refer2_1_y0));
  seg seg_1 (
    .A(refer2_1_y7), .B(refer2_1_y6), .C(refer2_1_y5), .D(refer2_1_y4), .out_5(out_6), .out_6(out_7),
    .out_7(out_8), .out_8(out_9), .out_9(out_10), .out_10(out_11), .out_11(out_12));
  seg seg_2 (
    .A(refer2_1_y3), .B(refer2_1_y2), .C(refer2_1_y1), .D(refer2_1_y0), .out_5(out_13), .out_6(out_14),
    .out_7(out_15), .out_8(out_16), .out_9(out_17), .out_10(out_18), .out_11(out_19));
endmodule

module control_8 (
  input  I7,
  input  I6,
  input  I5,
  input  I3,
  input  I2,
  input  I1,
  input  I0,
  output Y5,
  output Y4,
  output Y3,
  output Y2,
  output Y1,
  output Y0
);

  wire not_1_out;

  not not_1 (not_1_out, I3);
  and and_1 (Y5, I6, not_1_out);
  or or_1 (Y4, I6, I5);
  or or_2 (Y3, I6, I5, I3);
  or or_3 (Y2, I2, I3);
  or or_4 (Y1, I6, I5, I1);
  or or_5 (Y0, I1, I0);
endmodule

module counter_3 (
  input  in_1,
  output out_2,
  output out_3,
  output out_4
);

  wire clock_1_out, not_1_out, not_2_out;

  Clock clock_1 (.out(clock_1_out));
  not not_1 (not_1_out, out_2);
  not not_2 (not_2_out, out_3);
  T_Flip_Flop t_ff_1 (.clk(clock_1_out), .T(in_1), .Q(out_2));  // open: Qn, preset, reset, en
  T_Flip_Flop t_ff_2 (.clk(not_1_out), .T(in_1), .Q(out_3));  // open: Qn, preset, reset, en
  T_Flip_Flop t_ff_3 (.clk(not_2_out), .T(in_1), .Q(out_4));  // open: Qn, preset, reset, en
endmodule

module refer2 (
  input  A,
  input  B,
  input  C,
  input  D,
  input  E,
  output Y7,
  output Y6,
  output Y5,
  output Y4,
  output Y3,
  output Y2,
  output Y1,
  output Y0
);

  wire and_1_out, and_2_out, and_3_out, and_4_out, and_5_out, and_6_out, and_7_out, and_8_out, and_9_out,
       and_10_out, and_11_out, and_12_out, and_13_out, and_14_out, and_15_out, and_16_out, and_17_out,
       and_18_out, not_1_out, not_2_out, not_3_out, not_4_out, not_5_out, not_6_out, not_7_out, not_8_out,
       not_9_out, not_10_out, not_11_out, not_12_out, not_13_out, not_14_out, not_15_out, not_16_out,
       not_17_out, not_18_out, not_19_out, not_20_out, not_21_out, not_22_out, not_23_out, not_24_out,
       not_25_out;

  and and_1 (and_1_out, A, C);
  and and_2 (and_2_out, A, B);
  not not_1 (not_1_out, A);
  not not_2 (not_2_out, A);
  not not_3 (not_3_out, B);
  not not_4 (not_4_out, C);
  not not_5 (not_5_out, A);
  not not_6 (not_6_out, C);
  not not_7 (not_7_out, D);
  not not_8 (not_8_out, B);
  not not_9 (not_9_out, C);
  not not_10 (not_10_out, D);
  not not_11 (not_11_out, A);
  not not_12 (not_12_out, B);
  not not_13 (not_13_out, A);
  not not_14 (not_14_out, C);
  not not_15 (not_15_out, D);
  not not_16 (not_16_out, C);
  not not_17 (not_17_out, A);
  not not_18 (not_18_out, B);
  not not_19 (not_19_out, B);
  not not_20 (not_20_out, A);
  not not_21 (not_21_out, D);
  not not_22 (not_22_out, B);
  not not_23 (not_23_out, C);
  not not_24 (not_24_out, D);
  not not_25 (not_25_out, C);
  or or_1 (Y5, and_1_out, and_2_out);
  and and_3 (and_3_out, not_1_out, B, D);
  and and_4 (and_4_out, not_2_out, B, C);
  and and_5 (and_5_out, B, C, D);
  and and_6 (and_6_out, A, not_3_out, not_4_out);
  and and_7 (and_7_out, not_5_out, B, not_6_out, not_7_out);
  and and_8 (and_8_out, A, not_8_out, not_9_out, D);
  and and_9 (and_9_out, A, B, C, not_10_out);
  and and_10 (and_10_out, not_11_out, not_12_out, C);
  and and_11 (and_11_out, not_13_out, C, D);
  and and_12 (and_12_out, A, not_14_out, not_15_out);
  and and_13 (and_13_out, A, B, not_16_out);
  and and_14 (and_14_out, not_17_out, not_18_out, D);
  and and_15 (and_15_out, not_19_out, C, D);
  and and_16 (and_16_out, not_20_out, B, C, not_21_out);
  and and_17 (and_17_out, A, not_22_out, not_23_out, not_24_out);
  and and_18 (and_18_out, A, B, not_25_out, D);
  or or_2 (Y4, and_3_out, and_4_out, and_5_out, and_6_out);
  or or_3 (Y3, and_7_out, and_8_out, and_9_out);
  or or_4 (Y2, and_10_out, and_11_out, and_12_out, and_13_out);
  or or_5 (Y1, and_14_out, and_15_out, and_16_out, and_17_out, and_18_out);

  assign Y0 = E;
  assign Y6 = 1'b0;
  assign Y7 = 1'b0;
endmodule

module controler5 (
  input  in_1,
  input  in_2,
  input  in_3,
  input  in_4,
  input  in_5,
  input  in_6,
  output out_7,
  output out_8,
  output out_9,
  output out_10,
  output out_11
);

  assign out_7 = in_1 ? in_2 : 1'bz;  // Controlled_Buffer controlled_buffer_1
  assign out_8 = in_1 ? in_3 : 1'bz;  // Controlled_Buffer controlled_buffer_2
  assign out_9 = in_1 ? in_4 : 1'bz;  // Controlled_Buffer controlled_buffer_3
  assign out_10 = in_1 ? in_5 : 1'bz;  // Controlled_Buffer controlled_buffer_4
  assign out_11 = in_1 ? in_6 : 1'bz;  // Controlled_Buffer controlled_buffer_5
endmodule

module regisiter5 (
  input  in_1,
  input  in_2,
  input  in_3,
  input  in_4,
  input  in_5,
  input  in_6,
  output out_7,
  output out_8,
  output out_9,
  output out_10,
  output out_11
);

  D_Flip_Flop d_ff_1 (.clk(in_6), .D(in_1), .Q(out_7));  // open: Qn, preset, en, reset
  D_Flip_Flop d_ff_2 (.clk(in_6), .D(in_2), .Q(out_8));  // open: Qn, preset, en, reset
  D_Flip_Flop d_ff_3 (.clk(in_6), .D(in_3), .Q(out_9));  // open: Qn, preset, en, reset
  D_Flip_Flop d_ff_4 (.clk(in_6), .D(in_4), .Q(out_10));  // open: Qn, preset, en, reset
  D_Flip_Flop d_ff_5 (.clk(in_6), .D(in_5), .Q(out_11));  // open: Qn, preset, en, reset
endmodule

module sub (
  input  Cn_1,
  input  An,
  input  Bn,
  output Sn,
  output Cn
);

  wire ha_1_ci_1, ha_1_si, ha_2_ci_1;

  HA ha_1 (.Ai(An), .Bi(Bn), .Si(ha_1_si), .Ci_1(ha_1_ci_1));
  HA ha_2 (.Ai(Cn_1), .Bi(ha_1_si), .Si(Sn), .Ci_1(ha_2_ci_1));
  or or_1 (Cn, ha_2_ci_1, ha_1_ci_1);
endmodule

module add_sub (
  input  S,
  input  Cn_1,
  input  An,
  input  Bn,
  output Sn,
  output Cn
);

  wire and_1_out, and_2_out, xor_1_out, xor_2_out, xor_4_out;

  xor xor_1 (xor_1_out, S, An);
  xor xor_2 (xor_2_out, An, Bn);
  xor xor_3 (Sn, Cn_1, xor_2_out);
  xor xor_4 (xor_4_out, xor_1_out, Bn);
  and and_1 (and_1_out, xor_1_out, Bn);
  and and_2 (and_2_out, Cn_1, xor_4_out);
  or or_1 (Cn, and_2_out, and_1_out);
endmodule

module _4_add_sub (
  input  S,
  input  A3,
  input  A2,
  input  A1,
  input  A0,
  input  B3,
  input  B2,
  input  B1,
  input  B0,
  output Cn_1,
  output S3,
  output S2,
  output S1,
  output S0
);

  wire add_sub_1_cn, add_sub_2_cn, add_sub_3_cn;

  add_sub add_sub_1 (.Cn_1(1'b0), .An(A0), .Bn(B0), .S(S), .Sn(S0), .Cn(add_sub_1_cn));
  add_sub add_sub_2 (.Cn_1(add_sub_1_cn), .An(A1), .Bn(B1), .S(S), .Sn(S1), .Cn(add_sub_2_cn));
  add_sub add_sub_3 (.Cn_1(add_sub_2_cn), .An(A2), .Bn(B2), .S(S), .Sn(S2), .Cn(add_sub_3_cn));
  add_sub add_sub_4 (.Cn_1(add_sub_3_cn), .An(A3), .Bn(B3), .S(S), .Sn(S3), .Cn(Cn_1));
endmodule

module \手动加法器  (
  input  in_1,
  input  I0,
  input  I1,
  input  I2,
  input  I3,
  input  in_6,
  input  I4,
  input  I5,
  input  I6,
  input  I7,
  input  I8,
  input  I9,
  input  I10,
  input  I11,
  input  I12,
  input  I13,
  input  I14,
  input  I15,
  input  I0_2,
  input  I1_2,
  input  in_21,
  input  I2_2,
  input  in_23,
  input  I3_2,
  input  in_25,
  input  I4_2,
  input  in_27,
  input  I5_2,
  input  I6_2,
  input  I7_2,
  input  in_31,
  input  I8_2,
  input  I9_2,
  input  I10_2,
  input  I11_2,
  input  in_36,
  input  I12_2,
  input  I13_2,
  input  I14_2,
  input  I15_2
);

  wire controler_1_out_6, controler_1_out_7, controler_1_out_8, controler_1_out_9, controlled_buffer_1_out,
       n2_seg_1_out_6, n2_seg_1_out_7, n2_seg_1_out_8, n2_seg_1_out_9, n2_seg_1_out_10, n2_seg_1_out_11,
       n2_seg_1_out_12, n2_seg_1_out_13, n2_seg_1_out_14, n2_seg_1_out_15, n2_seg_1_out_16, n2_seg_1_out_17,
       n2_seg_1_out_18, n2_seg_1_out_19, n4_16_1_y0, n4_16_1_y1, n4_16_1_y2, n4_16_1_y3, n4_16_1_y4,
       n4_16_1_y5, n4_16_1_y6, n4_16_1_y7, n4_16_1_y8, n4_16_1_y9, n4_16_1_y10, n4_16_1_y11, n4_16_1_y12,
       n4_16_1_y13, n4_16_1_y14, n4_16_1_y15, n4_add_sub_1_cn_1, n4_add_sub_1_s0, n4_add_sub_1_s1,
       n4_add_sub_1_s2, n4_add_sub_1_s3, n16_4_1_z0, n16_4_1_z1, n16_4_1_z2, n16_4_1_z3, n16_4_2_z0,
       n16_4_2_z1, n16_4_2_z2, n16_4_2_z3, regisiter5_1_out_7, regisiter5_1_out_8, regisiter5_1_out_9,
       regisiter5_1_out_10, regisiter5_1_out_11, regisiter_1_out_6, regisiter_1_out_7, regisiter_1_out_8,
       regisiter_1_out_9, regisiter_2_out_6, regisiter_2_out_7, regisiter_2_out_8, regisiter_2_out_9;

  _16_4 u_16_4_1 (
    .A0(I0), .A1(I1), .A2(I2), .A3(I3), .A4(I4), .A5(I5), .A6(I6), .A7(I7), .A8(I8), .A9(I9), .A10(I10),
    .A11(I11), .A12(I12), .A13(I13), .A14(I14), .A15(I15), .Z0(n16_4_1_z0), .Z1(n16_4_1_z1), .Z2(n16_4_1_z2),
    .Z3(n16_4_1_z3));  // open: out_21
  _16_4 u_16_4_2 (
    .A0(I0_2), .A1(I1_2), .A2(I2_2), .A3(I3_2), .A4(I4_2), .A5(I5_2), .A6(I6_2), .A7(I7_2), .A8(I8_2),
    .A9(I9_2), .A10(I10_2), .A11(I11_2), .A12(I12_2), .A13(I13_2), .A14(I14_2), .A15(I15_2), .Z0(n16_4_2_z0),
    .Z1(n16_4_2_z1), .Z2(n16_4_2_z2), .Z3(n16_4_2_z3));  // open: out_21
  controler controler_1 (
    .in_2(n16_4_1_z0), .in_3(n16_4_1_z1), .in_4(n16_4_1_z2), .in_5(n16_4_1_z3), .in_1(in_6),
    .out_6(controler_1_out_6), .out_7(controler_1_out_7), .out_8(controler_1_out_8), .out_9(controler_1_out_9));
  controler controler_2 (
    .in_2(n16_4_2_z0), .in_3(n16_4_2_z1), .in_4(n16_4_2_z2), .in_5(n16_4_2_z3), .in_1(in_25),
    .out_6(controler_1_out_6), .out_7(controler_1_out_7), .out_8(controler_1_out_8), .out_9(controler_1_out_9));
  LED led_1 (.in(controler_1_out_6));
  LED led_2 (.in(controler_1_out_9));
  LED led_3 (.in(controler_1_out_8));
  LED led_4 (.in(controler_1_out_7));
  _2_seg u_2_seg_1 (
    .in_1(controlled_buffer_1_out), .in_2(controler_1_out_9), .in_3(controler_1_out_8),
    .in_4(controler_1_out_7), .in_5(controler_1_out_6), .out_6(n2_seg_1_out_6), .out_7(n2_seg_1_out_7),
    .out_8(n2_seg_1_out_8), .out_9(n2_seg_1_out_9), .out_10(n2_seg_1_out_10), .out_11(n2_seg_1_out_11),
    .out_12(n2_seg_1_out_12), .out_13(n2_seg_1_out_13), .out_14(n2_seg_1_out_14), .out_15(n2_seg_1_out_15),
    .out_16(n2_seg_1_out_16), .out_17(n2_seg_1_out_17), .out_18(n2_seg_1_out_18), .out_19(n2_seg_1_out_19));
  assign controlled_buffer_1_out = in_1 ? 1'b0 : 1'bz;  // Controlled_Buffer controlled_buffer_1
  regisiter regisiter_1 (
    .in_1(controler_1_out_9), .in_2(controler_1_out_8), .in_3(controler_1_out_7), .in_4(controler_1_out_6),
    .in_5(in_27), .out_6(regisiter_1_out_6), .out_7(regisiter_1_out_7), .out_8(regisiter_1_out_8),
    .out_9(regisiter_1_out_9));
  regisiter regisiter_2 (
    .in_1(controler_1_out_9), .in_2(controler_1_out_8), .in_3(controler_1_out_7), .in_4(controler_1_out_6),
    .in_5(in_36), .out_6(regisiter_2_out_6), .out_7(regisiter_2_out_7), .out_8(regisiter_2_out_8),
    .out_9(regisiter_2_out_9));
  _4_add_sub u_4_add_sub_1 (
    .A3(regisiter_1_out_6), .A2(regisiter_1_out_7), .A1(regisiter_1_out_8), .A0(regisiter_1_out_9),
    .B3(regisiter_2_out_6), .B2(regisiter_2_out_7), .B1(regisiter_2_out_8), .B0(regisiter_2_out_9),
    .Cn_1(n4_add_sub_1_cn_1), .S3(n4_add_sub_1_s3), .S2(n4_add_sub_1_s2), .S1(n4_add_sub_1_s1),
    .S0(n4_add_sub_1_s0), .S(in_21));
  _7_Segment_Display u_7_segment_display_1 (
    .g(n2_seg_1_out_19), .f(n2_seg_1_out_18), .a(n2_seg_1_out_13), .b(n2_seg_1_out_14), .e(n2_seg_1_out_17),
    .d(n2_seg_1_out_16), .c(n2_seg_1_out_15), .dp(1'b0));
  _7_Segment_Display u_7_segment_display_2 (
    .g(n2_seg_1_out_12), .f(n2_seg_1_out_11), .a(n2_seg_1_out_6), .b(n2_seg_1_out_7), .e(n2_seg_1_out_10),
    .d(n2_seg_1_out_9), .c(n2_seg_1_out_8), .dp(1'b0));
  regisiter5 regisiter5_1 (
    .in_1(n4_add_sub_1_cn_1), .in_2(n4_add_sub_1_s3), .in_3(n4_add_sub_1_s2), .in_4(n4_add_sub_1_s1),
    .in_5(n4_add_sub_1_s0), .in_6(in_31), .out_7(regisiter5_1_out_7), .out_8(regisiter5_1_out_8),
    .out_9(regisiter5_1_out_9), .out_10(regisiter5_1_out_10), .out_11(regisiter5_1_out_11));
  controler5 controler5_1 (
    .in_2(regisiter5_1_out_7), .in_3(regisiter5_1_out_8), .in_4(regisiter5_1_out_9),
    .in_5(regisiter5_1_out_10), .in_6(regisiter5_1_out_11), .in_1(in_23), .out_7(controlled_buffer_1_out),
    .out_8(controler_1_out_9), .out_9(controler_1_out_8), .out_10(controler_1_out_7),
    .out_11(controler_1_out_6));
  _4_16 u_4_16_1 (
    .A0(controler_1_out_6), .A1(controler_1_out_7), .A2(controler_1_out_8), .A3(controler_1_out_9),
    .Y0(n4_16_1_y0), .Y1(n4_16_1_y1), .Y2(n4_16_1_y2), .Y3(n4_16_1_y3), .Y4(n4_16_1_y4), .Y5(n4_16_1_y5),
    .Y6(n4_16_1_y6), .Y7(n4_16_1_y7), .Y8(n4_16_1_y8), .Y9(n4_16_1_y9), .Y10(n4_16_1_y10), .Y11(n4_16_1_y11),
    .Y12(n4_16_1_y12), .Y13(n4_16_1_y13), .Y14(n4_16_1_y14), .Y15(n4_16_1_y15));
  LED led_5 (.in(n4_16_1_y0));
  LED led_6 (.in(n4_16_1_y1));
  LED led_7 (.in(n4_16_1_y2));
  LED led_8 (.in(n4_16_1_y3));
  LED led_9 (.in(n4_16_1_y4));
  LED led_10 (.in(n4_16_1_y5));
  LED led_11 (.in(n4_16_1_y6));
  LED led_12 (.in(n4_16_1_y7));
  LED led_13 (.in(n4_16_1_y8));
  LED led_14 (.in(n4_16_1_y9));
  LED led_15 (.in(n4_16_1_y10));
  LED led_16 (.in(n4_16_1_y11));
  LED led_17 (.in(n4_16_1_y12));
  LED led_18 (.in(n4_16_1_y13));
  LED led_19 (.in(n4_16_1_y14));
  LED led_20 (.in(n4_16_1_y15));
endmodule

module \跑马灯  (
  input  in_1,
  output out_2,
  output out_3,
  output out_4,
  output out_5,
  output out_6,
  output out_7,
  output out_8,
  output out_9,
  output out_10,
  output out_11,
  output out_12,
  output out_13,
  output out_14,
  output out_15,
  output out_16,
  output out_17
);

  wire counter_1_out_2, counter_1_out_3, counter_1_out_4, counter_1_out_5;

  counter counter_1 (
    .out_2(counter_1_out_2), .out_3(counter_1_out_3), .out_4(counter_1_out_4), .out_5(counter_1_out_5),
    .in_1(in_1));
  _4_16 u_4_16_1 (
    .A0(counter_1_out_2), .A1(counter_1_out_3), .A2(counter_1_out_4), .A3(counter_1_out_5), .Y0(out_2),
    .Y1(out_3), .Y2(out_4), .Y3(out_5), .Y4(out_6), .Y5(out_7), .Y6(out_8), .Y7(out_9), .Y8(out_10),
    .Y9(out_11), .Y10(out_12), .Y11(out_13), .Y12(out_14), .Y13(out_15), .Y14(out_16), .Y15(out_17));
endmodule
