// Logisim project 16-4.circ as structural Verilog
// 8-3
module _8_3prior (
  input  I0_prime,
  input  I1_prime,
  input  I2_prime,
  input  I3_prime,
  input  I4_prime,
  input  I5_prime,
  input  I6_prime,
  input  I7_prime,
  input  S_prime,
  output Ys_prime,
  output Yex_prime,
  output Y0_prime,
  output Y1_prime,
  output Y2_prime
);

  wire and_1_out, and_2_out, and_3_out, and_4_out, and_5_out, and_6_out, and_7_out, and_8_out, and_9_out,
       and_10_out, and_11_out, and_12_out, not_1_out, not_2_out, not_3_out, not_4_out, not_5_out, not_6_out,
       not_7_out, not_8_out, not_9_out, not_10_out, not_11_out, not_12_out;

  not not_1 (not_1_out, I1_prime);
  not not_2 (not_2_out, I2_prime);
  not not_3 (not_3_out, I3_prime);
  not not_4 (not_4_out, I4_prime);
  not not_5 (not_5_out, I5_prime);
  not not_6 (not_6_out, I6_prime);
  not not_7 (not_7_out, I7_prime);
  not not_8 (not_8_out, S_prime);
  not not_9 (not_9_out, not_2_out);
  not not_10 (not_10_out, not_4_out);
  not not_11 (not_11_out, not_5_out);
  not not_12 (not_12_out, not_6_out);
  and and_1 (and_1_out, not_1_out, not_9_out, not_10_out, not_12_out, not_8_out);
  and and_2 (and_2_out, not_3_out, not_10_out, not_12_out, not_8_out);
  and and_3 (and_3_out, not_5_out, not_12_out, not_8_out);
  and and_4 (and_4_out, not_7_out, not_8_out);
  and and_5 (and_5_out, not_2_out, not_10_out, not_11_out, not_8_out);
  and and_6 (and_6_out, not_3_out, not_10_out, not_11_out, not_8_out);
  and and_7 (and_7_out, not_6_out, not_8_out);
  and and_8 (and_8_out, not_7_out, not_8_out);
  and and_9 (and_9_out, not_4_out, not_8_out);
  and and_10 (and_10_out, not_5_out, not_8_out);
  and and_11 (and_11_out, not_6_out, not_8_out);
  and and_12 (and_12_out, not_7_out, not_8_out);
  nand nand_1 (Ys_prime, I0_prime, I1_prime, I2_prime, I3_prime, I4_prime, I5_prime, I6_prime, I7_prime, not_8_out);
  nand nand_2 (Yex_prime, Ys_prime, not_8_out);
  nor nor_1 (Y0_prime, and_1_out, and_2_out, and_3_out, and_4_out);
  nor nor_2 (Y1_prime, and_5_out, and_6_out, and_7_out, and_8_out);
  nor nor_3 (Y2_prime, and_9_out, and_10_out, and_11_out, and_12_out);
endmodule

module _16_4 (
  input  A0,
  input  A1,
  input  A2,
  input  A3,
  input  A4,
  input  A5,
  input  A6,
  input  A7,
  input  A8,
  input  A9,
  input  A10,
  input  A11,
  input  A12,
  input  A13,
  input  A14,
  input  A15,
  output Z3,
  output Z2,
  output Z1,
  output Z0
);

  wire n8_3prior_1_y0_prime, n8_3prior_1_y1_prime, n8_3prior_1_y2_prime, n8_3prior_2_y0_prime,
       n8_3prior_2_y1_prime, n8_3prior_2_y2_prime, n8_3prior_2_yex_prime, n8_3prior_2_ys_prime, not_1_out,
       not_2_out, not_3_out, not_4_out, not_5_out, not_6_out, not_7_out, not_8_out, not_9_out, not_10_out,
       not_11_out, not_12_out, not_13_out, not_14_out, not_15_out, not_16_out;

  not not_1 (not_1_out, A0);
  not not_2 (not_2_out, A1);
  not not_3 (not_3_out, A2);
  not not_4 (not_4_out, A3);
  not not_5 (not_5_out, A4);
  not not_6 (not_6_out, A5);
  not not_7 (not_7_out, A6);
  not not_8 (not_8_out, A7);
  not not_9 (not_9_out, A8);
  not not_10 (not_10_out, A9);
  not not_11 (not_11_out, A10);
  not not_12 (not_12_out, A11);
  not not_13 (not_13_out, A12);
  not not_14 (not_14_out, A13);
  not not_15 (not_15_out, A14);
  not not_16 (not_16_out, A15);
  _8_3prior u_8_3prior_1 (
    .I0_prime(not_1_out), .I1_prime(not_2_out), .I2_prime(not_3_out), .I3_prime(not_4_out),
    .I4_prime(not_5_out), .I5_prime(not_6_out), .I6_prime(not_7_out), .I7_prime(not_8_out),
    .S_prime(n8_3prior_2_ys_prime), .Y0_prime(n8_3prior_1_y0_prime), .Y1_prime(n8_3prior_1_y1_prime),
    .Y2_prime(n8_3prior_1_y2_prime));  // open: Ys_prime, Yex_prime
  _8_3prior u_8_3prior_2 (
    .I0_prime(not_9_out), .I1_prime(not_10_out), .I2_prime(not_11_out), .I3_prime(not_12_out),
    .I4_prime(not_13_out), .I5_prime(not_14_out), .I6_prime(not_15_out), .I7_prime(not_16_out),
    .S_prime(1'b0), .Ys_prime(n8_3prior_2_ys_prime), .Yex_prime(n8_3prior_2_yex_prime),
    .Y0_prime(n8_3prior_2_y0_prime), .Y1_prime(n8_3prior_2_y1_prime), .Y2_prime(n8_3prior_2_y2_prime));
  nand nand_1 (Z0, n8_3prior_1_y0_prime, n8_3prior_2_y0_prime);
  nand nand_2 (Z1, n8_3prior_1_y1_prime, n8_3prior_2_y1_prime);
  nand nand_3 (Z2, n8_3prior_1_y2_prime, n8_3prior_2_y2_prime);
  not not_17 (Z3, n8_3prior_2_yex_prime);
endmodule
