// Logisim project 4-16.circ as structural Verilog: 3 circuits, main circuit main
// 4-16
module main (
  input  in_1,
  input  in_2,
  input  in_3,
  input  in_4,
  output out_5,
  output out_6,
  output out_7,
  output out_8,
  output out_9,
  output out_10,
  output out_11,
  output out_12,
  output out_13,
  output out_14,
  output out_15,
  output out_16,
  output out_17,
  output out_18,
  output out_19,
  output out_20
);

  wire and_1_out, and_2_out, and_3_out, and_4_out, n138_1_out_4, n138_1_out_5, n138_1_out_6, n138_1_out_7,
       n138_1_out_8, n138_1_out_9, n138_1_out_10, n138_1_out_11, n138_2_out_4, n138_2_out_5, n138_2_out_6,
       n138_2_out_7, n138_2_out_8, n138_2_out_9, n138_2_out_10, n138_2_out_11, not_1_out, not_2_out;

  not not_1 (not_1_out, in_2);
  _138 u_138_1 (
    .in_1(in_4), .in_2(in_3), .in_3(in_2), .out_4(n138_1_out_4), .out_5(n138_1_out_5), .out_6(n138_1_out_6),
    .out_7(n138_1_out_7), .out_8(n138_1_out_8), .out_9(n138_1_out_9), .out_10(n138_1_out_10),
    .out_11(n138_1_out_11));
  _138 u_138_2 (
    .in_1(in_4), .in_2(in_3), .in_3(in_2), .out_4(n138_2_out_4), .out_5(n138_2_out_5), .out_6(n138_2_out_6),
    .out_7(n138_2_out_7), .out_8(n138_2_out_8), .out_9(n138_2_out_9), .out_10(n138_2_out_10),
    .out_11(n138_2_out_11));
  not not_2 (not_2_out, in_1);
  and and_1 (and_1_out, not_2_out, not_1_out);
  and and_2 (and_2_out, not_2_out, in_2);
  and and_3 (and_3_out, in_2, in_1);
  c4 c4_1 (
    .in_2(n138_2_out_4), .in_3(n138_2_out_5), .in_4(n138_2_out_6), .in_5(n138_2_out_7), .in_1(and_1_out),
    .out_6(out_5), .out_7(out_6), .out_8(out_7), .out_9(out_8));
  c4 c4_2 (
    .in_2(n138_2_out_8), .in_3(n138_2_out_9), .in_4(n138_2_out_10), .in_5(n138_2_out_11), .in_1(and_2_out),
    .out_6(out_9), .out_7(out_10), .out_8(out_11), .out_9(out_12));
  and and_4 (and_4_out, in_1, not_1_out);
  c4 c4_3 (
    .in_2(n138_1_out_4), .in_3(n138_1_out_5), .in_4(n138_1_out_6), .in_5(n138_1_out_7), .in_1(and_4_out),
    .out_6(out_13), .out_7(out_14), .out_8(out_15), .out_9(out_16));
  c4 c4_4 (
    .in_2(n138_1_out_8), .in_3(n138_1_out_9), .in_4(n138_1_out_10), .in_5(n138_1_out_11), .in_1(and_3_out),
    .out_6(out_17), .out_7(out_18), .out_8(out_19), .out_9(out_20));
endmodule

// 3-8
module _138 (
  input  in_1,
  input  in_2,
  input  in_3,
  output out_4,
  output out_5,
  output out_6,
  output out_7,
  output out_8,
  output out_9,
  output out_10,
  output out_11
);

  wire not_1_out, not_2_out, not_3_out;

  not not_1 (not_1_out, in_1);
  not not_2 (not_2_out, in_2);
  not not_3 (not_3_out, in_3);
  and and_1 (out_4, not_1_out, not_2_out, not_3_out);
  and and_2 (out_5, in_1, not_2_out, not_3_out);
  and and_3 (out_6, not_1_out, in_2, not_3_out);
  and and_4 (out_7, in_1, in_2, not_3_out);
  and and_5 (out_8, not_1_out, not_2_out, in_3);
  and and_6 (out_9, in_1, not_2_out, in_3);
  and and_7 (out_10, not_1_out, in_2, in_3);
  and and_8 (out_11, in_1, in_2, in_3);
endmodule

module c4 (
  input  in_1,
  input  in_2,
  input  in_3,
  input  in_4,
  input  in_5,
  output out_6,
  output out_7,
  output out_8,
  output out_9
);

  assign out_6 = in_1 ? in_2 : 1'bz;  // Controlled_Buffer controlled_buffer_1
  assign out_7 = in_1 ? in_3 : 1'bz;  // Controlled_Buffer controlled_buffer_2
  assign out_8 = in_1 ? in_4 : 1'bz;  // Controlled_Buffer controlled_buffer_3
  assign out_9 = in_1 ? in_5 : 1'bz;  // Controlled_Buffer controlled_buffer_4
endmodule
