// Logisim project ALU.circ as structural Verilog: 7 circuits, main circuit main
// ALU
module main (
  input  [2:0] OP,
  input  [7:0] A,
  input  [7:0] B,
  input  LOAD,
  input  in_5,
  output [7:0] result,
  output [7:0] \乘积低位 
);

  wire n138_1_out_4, n138_1_out_5, n138_1_out_6, n138_1_out_7, n138_1_out_8, n138_1_out_9, n138_1_out_10,
       n138_1_out_11;
  wire [7:0] and_1_out, n8adder_1_s, not_1_out, or_1_out, shl_1_result, shr_1_result, sub_1_result;
  wire [15:0] mul_1_out_5;

  shl shl_1 (.A(A), .result(shl_1_result));
  shr shr_1 (.A(A), .result(shr_1_result));
  mul mul_1 (.\被乘数 (A), .\乘数 (B), .out_5(mul_1_out_5), .in_3(LOAD), .in_4(in_5));
  assign not_1_out = ~A;  // NOT_Gate not_1, 8 bits wide
  assign or_1_out = A | B;  // OR_Gate or_1, 8 bits wide
  assign and_1_out = A & B;  // AND_Gate and_1, 8 bits wide
  _8Adder u_8adder_1 (.B(A), .A(B), .S(n8adder_1_s));  // open: C
  sub sub_1 (.A(A), .B(B), .result(sub_1_result));  // open: carryout
  _138 u_138_1 (
    .in_1(OP[0]), .in_2(OP[1]), .in_3(OP[2]), .out_4(n138_1_out_4), .out_5(n138_1_out_5),
    .out_6(n138_1_out_6), .out_7(n138_1_out_7), .out_8(n138_1_out_8), .out_9(n138_1_out_9),
    .out_10(n138_1_out_10), .out_11(n138_1_out_11));
  assign result = n138_1_out_4 ? not_1_out : 8'bz;  // Controlled_Buffer controlled_buffer_1
  assign result = n138_1_out_5 ? or_1_out : 8'bz;  // Controlled_Buffer controlled_buffer_2
  assign result = n138_1_out_6 ? and_1_out : 8'bz;  // Controlled_Buffer controlled_buffer_3
  assign result = n138_1_out_7 ? shl_1_result : 8'bz;  // Controlled_Buffer controlled_buffer_4
  assign result = n138_1_out_8 ? shr_1_result : 8'bz;  // Controlled_Buffer controlled_buffer_5
  assign result = n138_1_out_9 ? n8adder_1_s : 8'bz;  // Controlled_Buffer controlled_buffer_6
  assign result = n138_1_out_10 ? sub_1_result : 8'bz;  // Controlled_Buffer controlled_buffer_7
  assign {result, \乘积低位 } = n138_1_out_11 ? mul_1_out_5 : 16'bz;  // Controlled_Buffer controlled_buffer_8
endmodule

module sub (
  input  [7:0] A,
  input  [7:0] B,
  output [7:0] result,
  output carryout
);

  wire [7:0] n8adder_1_s, not_1_out;

  _8Adder u_8adder_1 (.B(not_1_out), .A(8'h1), .S(n8adder_1_s));  // open: C
  assign not_1_out = ~B;  // NOT_Gate not_1, 8 bits wide
  _8Adder u_8adder_2 (.B(A), .A(n8adder_1_s), .C(carryout), .S(result));
endmodule

module shl (
  input  [7:0] A,
  output [7:0] result
);


  assign result = {A[6:0], 1'b0};
endmodule

module shr (
  input  [7:0] A,
  output [7:0] result
);


  assign result = {1'b0, A[7:1]};
endmodule

module mul (
  input  [7:0] \被乘数 ,
  input  [7:0] \乘数 ,
  input  in_3,
  input  in_4,
  output [15:0] out_5
);

  wire [7:0] multiplexer_1_out, multiplexer_2_out, n8adder_1_s;

  Multiplexer #(.width(8), .enable("false")) multiplexer_1 (
    .in0({8{1'b0}}), .in1(\被乘数 ), .out(multiplexer_1_out), .sel(out_5[0]));
  _8Adder u_8adder_1 (.B(multiplexer_1_out), .A(out_5[15:8]), .S(n8adder_1_s));  // open: C
  Multiplexer #(.width(8), .enable("false")) multiplexer_2 (
    .in0({n8adder_1_s[0], out_5[7:1]}), .in1(\乘数 ), .out(multiplexer_2_out), .sel(in_3));
  reg8 reg8_1 (
    .in_1(n8adder_1_s[1]), .in_2(n8adder_1_s[2]), .in_3(n8adder_1_s[3]), .in_4(n8adder_1_s[4]),
    .in_5(n8adder_1_s[5]), .in_6(n8adder_1_s[6]), .in_7(n8adder_1_s[7]), .in_9(1'b0), .in_8(in_4),
    .out_10(out_5[8]), .out_11(out_5[9]), .out_12(out_5[10]), .out_13(out_5[11]), .out_14(out_5[12]),
    .out_15(out_5[13]), .out_16(out_5[14]), .out_17(out_5[15]));
  reg8 reg8_2 (
    .in_1(multiplexer_2_out[0]), .in_2(multiplexer_2_out[1]), .in_3(multiplexer_2_out[2]),
    .in_4(multiplexer_2_out[3]), .in_5(multiplexer_2_out[4]), .in_6(multiplexer_2_out[5]),
    .in_7(multiplexer_2_out[6]), .in_9(multiplexer_2_out[7]), .in_8(in_4), .out_10(out_5[0]),
    .out_11(out_5[1]), .out_12(out_5[2]), .out_13(out_5[3]), .out_14(out_5[4]), .out_15(out_5[5]),
    .out_16(out_5[6]), .out_17(out_5[7]));
endmodule

module _16reg (
  input  _0,
  input  in_2,
  input  in_3,
  input  in_4,
  input  in_5,
  input  in_6,
  input  in_7,
  input  in_8,
  input  in_9,
  input  in_10,
  input  in_11,
  input  in_12,
  input  in_13,
  input  in_14,
  input  in_15,
  input  in_16,
  input  in_17,
  output _0_2,
  output out_19,
  output out_20,
  output out_21,
  output out_22,
  output out_23,
  output out_24,
  output out_25,
  output out_26,
  output out_27,
  output out_28,
  output out_29,
  output out_30,
  output out_31,
  output out_32,
  output out_33
);

  Register #(.width(16)) register_1 (
    .D({in_17, in_16, in_15, in_14, in_13, in_11, in_10, in_9, in_8, in_7, in_6, in_5, in_4, in_3, in_2, _0}),
    .Q({out_33, out_32, out_31, out_30, out_29, out_28, out_27, out_26, out_25, out_24, out_23, out_22, out_21, out_20, out_19, _0_2}),
    .clk(in_12));  // open: en, clr
endmodule

module c16 (
  input  in_1,
  input  in_2,
  input  in_3,
  input  in_4,
  input  in_5,
  input  in_6,
  input  in_7,
  input  in_8,
  input  in_9,
  input  in_10,
  input  in_11,
  input  in_12,
  input  in_13,
  input  in_14,
  input  in_15,
  input  in_16,
  input  in_17,
  output out_18,
  output out_19,
  output out_20,
  output out_21,
  output out_22,
  output out_23,
  output out_24,
  output out_25,
  output out_26,
  output out_27,
  output out_28,
  output out_29,
  output out_30,
  output out_31,
  output out_32,
  output out_33
);

  assign out_18 = in_1 ? in_2 : 1'bz;  // Controlled_Buffer controlled_buffer_1
  assign out_19 = in_1 ? in_3 : 1'bz;  // Controlled_Buffer controlled_buffer_2
  assign out_20 = in_1 ? in_4 : 1'bz;  // Controlled_Buffer controlled_buffer_3
  assign out_21 = in_1 ? in_5 : 1'bz;  // Controlled_Buffer controlled_buffer_4
  assign out_22 = in_1 ? in_6 : 1'bz;  // Controlled_Buffer controlled_buffer_5
  assign out_23 = in_1 ? in_7 : 1'bz;  // Controlled_Buffer controlled_buffer_6
  assign out_24 = in_1 ? in_8 : 1'bz;  // Controlled_Buffer controlled_buffer_7
  assign out_25 = in_1 ? in_9 : 1'bz;  // Controlled_Buffer controlled_buffer_8
  assign out_26 = in_1 ? in_10 : 1'bz;  // Controlled_Buffer controlled_buffer_9
  assign out_27 = in_1 ? in_11 : 1'bz;  // Controlled_Buffer controlled_buffer_10
  assign out_28 = in_1 ? in_12 : 1'bz;  // Controlled_Buffer controlled_buffer_11
  assign out_29 = in_1 ? in_13 : 1'bz;  // Controlled_Buffer controlled_buffer_12
  assign out_30 = in_1 ? in_14 : 1'bz;  // Controlled_Buffer controlled_buffer_13
  assign out_31 = in_1 ? in_15 : 1'bz;  // Controlled_Buffer controlled_buffer_14
  assign out_32 = in_1 ? in_16 : 1'bz;  // Controlled_Buffer controlled_buffer_15
  assign out_33 = in_1 ? in_17 : 1'bz;  // Controlled_Buffer controlled_buffer_16
endmodule
