// Logisim project 加法器.circ as structural Verilog
module HA (
  input  A,
  input  B,
  output S,
  output C
);

  wire and_2_out, and_3_out, not_1_out, not_2_out;

  not not_1 (not_1_out, A);
  not not_2 (not_2_out, B);
  and and_1 (C, A, B);
  and and_2 (and_2_out, not_1_out, B);
  and and_3 (and_3_out, A, not_2_out);
  or or_1 (S, and_2_out, and_3_out);
endmodule

module FA (
  input  Cin,
  input  B,
  input  A,
  output Sum,
  output Cout
);

  wire ha_1_c, ha_1_s, ha_2_c;

  HA ha_1 (.A(B), .B(A), .S(ha_1_s), .C(ha_1_c));
  HA ha_2 (.A(Cin), .B(ha_1_s), .S(Sum), .C(ha_2_c));
  or or_1 (Cout, ha_2_c, ha_1_c);
endmodule

// add
module _8Adder (
  input  [7:0] B,
  input  [7:0] A,
  output [7:0] S,
  output C
);

  wire fa_1_cout, fa_2_cout, fa_3_cout, fa_4_cout, fa_5_cout, fa_6_cout, fa_7_cout;

  FA fa_1 (.Cin(1'b0), .B(B[0]), .A(A[0]), .Sum(S[0]), .Cout(fa_1_cout));
  FA fa_2 (.Cin(fa_3_cout), .B(B[2]), .A(A[2]), .Sum(S[2]), .Cout(fa_2_cout));
  FA fa_3 (.Cin(fa_1_cout), .B(B[1]), .A(A[1]), .Sum(S[1]), .Cout(fa_3_cout));
  FA fa_4 (.Cin(fa_2_cout), .B(B[3]), .A(A[3]), .Sum(S[3]), .Cout(fa_4_cout));
  FA fa_5 (.Cin(fa_6_cout), .B(B[5]), .A(A[5]), .Sum(S[5]), .Cout(fa_5_cout));
  FA fa_6 (.Cin(fa_4_cout), .B(B[4]), .A(A[4]), .Sum(S[4]), .Cout(fa_6_cout));
  FA fa_7 (.Cin(fa_5_cout), .B(B[6]), .A(A[6]), .Sum(S[6]), .Cout(fa_7_cout));
  FA fa_8 (.Cin(fa_7_cout), .B(B[7]), .A(A[7]), .Sum(S[7]), .Cout(C));
endmodule
