// Logisim project 多端口输入.circ as structural Verilog: 4 circuits, main circuit main
module main (
  input  I0,
  input  I1,
  input  in_3,
  input  in_4,
  input  I2,
  input  I3,
  input  I4,
  input  I5,
  input  I6,
  input  I7,
  input  I8,
  input  I9,
  input  I10,
  input  I11,
  input  in_15,
  input  I12,
  input  I13,
  input  I14,
  input  I15,
  input  I0_2,
  input  I1_2,
  input  I2_2,
  input  in_23,
  input  in_24,
  input  I3_2,
  input  I4_2,
  input  I5_2,
  input  I6_2,
  input  I7_2,
  input  I8_2,
  input  I9_2,
  input  I10_2,
  input  I11_2,
  input  I12_2,
  input  I13_2,
  input  I14_2,
  input  I15_2
);

  wire double_16key_1_out_37, double_16key_1_out_38, double_16key_1_out_39, double_16key_1_out_40,
       double_16key_1_out_41, double_16key_1_out_42, double_16key_1_out_43, double_16key_1_out_44,
       n2seg_1_out_10, n2seg_1_out_11, n2seg_1_out_12, n2seg_1_out_13, n2seg_1_out_14, n2seg_1_out_15,
       n2seg_1_out_16, n2seg_1_out_17, n2seg_1_out_18, n2seg_1_out_19, n2seg_1_out_20, n2seg_1_out_21,
       n2seg_1_out_22, n2seg_1_out_23;

  double_16key double_16key_1 (
    .I0(I0), .I1(I1), .I2(I2), .I3(I3), .I4(I4), .I5(I5), .I6(I6), .I7(I7), .I8(I8), .I9(I9), .I10(I10),
    .I11(I11), .I12(I12), .I13(I13), .I14(I14), .I15(I15), .I0_2(I0_2), .I1_2(I1_2), .I2_2(I2_2),
    .I3_2(I3_2), .I4_2(I4_2), .I5_2(I5_2), .I6_2(I6_2), .I7_2(I7_2), .I8_2(I8_2), .I9_2(I9_2), .I10_2(I10_2),
    .I11_2(I11_2), .I12_2(I12_2), .I13_2(I13_2), .I14_2(I14_2), .I15_2(I15_2), .in_13(in_3), .in_14(in_4),
    .in_34(in_23), .in_35(in_24), .out_37(double_16key_1_out_37), .out_38(double_16key_1_out_38),
    .out_39(double_16key_1_out_39), .out_40(double_16key_1_out_40), .out_41(double_16key_1_out_41),
    .out_42(double_16key_1_out_42), .out_43(double_16key_1_out_43), .out_44(double_16key_1_out_44));
  LED led_1 (.in(double_16key_1_out_41));
  LED led_2 (.in(double_16key_1_out_37));
  LED led_3 (.in(double_16key_1_out_38));
  LED led_4 (.in(double_16key_1_out_42));
  LED led_5 (.in(double_16key_1_out_39));
  LED led_6 (.in(double_16key_1_out_40));
  LED led_7 (.in(double_16key_1_out_43));
  LED led_8 (.in(double_16key_1_out_44));
  _2Seg u_2seg_1 (
    .in_1(double_16key_1_out_37), .in_3(double_16key_1_out_38), .in_4(double_16key_1_out_39),
    .in_5(double_16key_1_out_40), .in_6(double_16key_1_out_41), .in_7(double_16key_1_out_42),
    .in_8(double_16key_1_out_43), .in_9(double_16key_1_out_44), .in_2(in_15), .out_10(n2seg_1_out_10),
    .out_11(n2seg_1_out_11), .out_12(n2seg_1_out_12), .out_13(n2seg_1_out_13), .out_14(n2seg_1_out_14),
    .out_15(n2seg_1_out_15), .out_16(n2seg_1_out_16), .out_17(n2seg_1_out_17), .out_18(n2seg_1_out_18),
    .out_19(n2seg_1_out_19), .out_20(n2seg_1_out_20), .out_21(n2seg_1_out_21), .out_22(n2seg_1_out_22),
    .out_23(n2seg_1_out_23));
  _7_Segment_Display #(.active("false")) u_7_segment_display_1 (
    .g(n2seg_1_out_16), .f(n2seg_1_out_15), .a(n2seg_1_out_10), .b(n2seg_1_out_11), .e(n2seg_1_out_14),
    .d(n2seg_1_out_13), .c(n2seg_1_out_12), .dp(1'b1));
  _7_Segment_Display #(.active("false")) u_7_segment_display_2 (
    .g(n2seg_1_out_23), .f(n2seg_1_out_22), .a(n2seg_1_out_17), .b(n2seg_1_out_18), .e(n2seg_1_out_21),
    .d(n2seg_1_out_20), .c(n2seg_1_out_19), .dp(1'b1));
endmodule

module _16key (
  input  I0,
  input  I1,
  input  I2,
  input  I3,
  input  I4,
  input  I5,
  input  I6,
  input  I7,
  input  I8,
  input  I9,
  input  I10,
  input  I11,
  input  I12,
  input  in_14,
  input  I13,
  input  I14,
  input  I15,
  input  I0_2,
  input  I1_2,
  input  I2_2,
  input  I3_2,
  input  I4_2,
  input  I5_2,
  input  I6_2,
  input  I7_2,
  input  I8_2,
  input  I9_2,
  input  I10_2,
  input  I11_2,
  input  I12_2,
  input  I13_2,
  input  I14_2,
  input  I15_2,
  output out_34,
  output out_35,
  output out_36,
  output \低位 ,
  output out_38,
  output out_39,
  output out_40,
  output out_41
);

  wire n16_4_1_z0, n16_4_1_z1, n16_4_1_z2, n16_4_1_z3, n16_4_2_z0, n16_4_2_z1, n16_4_2_z2, n16_4_2_z3;

  _16_4 u_16_4_1 (
    .A0(I0), .A1(I1), .A2(I2), .A3(I3), .A4(I4), .A5(I5), .A6(I6), .A7(I7), .A8(I8), .A9(I9), .A10(I10),
    .A11(I11), .A12(I12), .A13(I13), .A14(I14), .A15(I15), .Z3(n16_4_1_z3), .Z2(n16_4_1_z2), .Z1(n16_4_1_z1),
    .Z0(n16_4_1_z0));
  _16_4 u_16_4_2 (
    .A0(I0_2), .A1(I1_2), .A2(I2_2), .A3(I3_2), .A4(I4_2), .A5(I5_2), .A6(I6_2), .A7(I7_2), .A8(I8_2),
    .A9(I9_2), .A10(I10_2), .A11(I11_2), .A12(I12_2), .A13(I13_2), .A14(I14_2), .A15(I15_2), .Z3(n16_4_2_z3),
    .Z2(n16_4_2_z2), .Z1(n16_4_2_z1), .Z0(n16_4_2_z0));
  c8 c8_1 (
    .in_2(n16_4_1_z3), .in_3(n16_4_1_z2), .in_4(n16_4_1_z1), .in_5(n16_4_1_z0), .in_6(n16_4_2_z3),
    .in_7(n16_4_2_z2), .in_8(n16_4_2_z1), .in_9(n16_4_2_z0), .in_1(in_14), .out_10(out_34), .out_11(out_35),
    .out_12(out_36), .out_13(\低位 ), .out_14(out_38), .out_15(out_39), .out_16(out_40), .out_17(out_41));
endmodule

module double_16key (
  input  I0,
  input  I1,
  input  I2,
  input  I3,
  input  I4,
  input  I5,
  input  I6,
  input  I7,
  input  I8,
  input  I9,
  input  I10,
  input  I11,
  input  in_13,
  input  in_14,
  input  I12,
  input  I13,
  input  I14,
  input  I15,
  input  I0_2,
  input  I1_2,
  input  I2_2,
  input  I3_2,
  input  I4_2,
  input  I5_2,
  input  I6_2,
  input  I7_2,
  input  I8_2,
  input  I9_2,
  input  I10_2,
  input  I11_2,
  input  I12_2,
  input  I13_2,
  input  I14_2,
  input  in_34,
  input  in_35,
  input  I15_2,
  output out_37,
  output out_38,
  output out_39,
  output out_40,
  output out_41,
  output out_42,
  output out_43,
  output out_44
);

  wire and_1_out, n16_4_1_z0, n16_4_1_z1, n16_4_1_z2, n16_4_1_z3, n16_4_2_z0, n16_4_2_z1, n16_4_2_z2,
       n16_4_2_z3, reg8_1_out_10, reg8_1_out_11, reg8_1_out_12, reg8_1_out_13, reg8_1_out_14, reg8_1_out_15,
       reg8_1_out_16, reg8_1_out_17;

  _16_4 u_16_4_1 (
    .A0(I0), .A1(I1), .A2(I2), .A3(I3), .A4(I4), .A5(I5), .A6(I6), .A7(I7), .A8(I8), .A9(I9), .A10(I10),
    .A11(I11), .A12(I12), .A13(I13), .A14(I14), .A15(I15), .Z3(n16_4_1_z3), .Z2(n16_4_1_z2), .Z1(n16_4_1_z1),
    .Z0(n16_4_1_z0));
  _16_4 u_16_4_2 (
    .A0(I0_2), .A1(I1_2), .A2(I2_2), .A3(I3_2), .A4(I4_2), .A5(I5_2), .A6(I6_2), .A7(I7_2), .A8(I8_2),
    .A9(I9_2), .A10(I10_2), .A11(I11_2), .A12(I12_2), .A13(I13_2), .A14(I14_2), .A15(I15_2), .Z3(n16_4_2_z3),
    .Z2(n16_4_2_z2), .Z1(n16_4_2_z1), .Z0(n16_4_2_z0));
  c8 c8_1 (
    .in_2(n16_4_1_z3), .in_3(n16_4_1_z2), .in_4(n16_4_1_z1), .in_5(n16_4_1_z0), .in_6(n16_4_2_z3),
    .in_7(n16_4_2_z2), .in_8(n16_4_2_z1), .in_9(n16_4_2_z0), .in_1(in_13), .out_10(out_37), .out_11(out_38),
    .out_12(out_39), .out_13(out_40), .out_14(out_41), .out_15(out_42), .out_16(out_43), .out_17(out_44));
  reg8 reg8_1 (
    .in_1(n16_4_1_z3), .in_2(n16_4_1_z2), .in_3(n16_4_1_z1), .in_4(n16_4_1_z0), .in_5(n16_4_2_z3),
    .in_6(n16_4_2_z2), .in_7(n16_4_2_z1), .in_9(n16_4_2_z0), .in_8(in_34), .out_10(reg8_1_out_10),
    .out_11(reg8_1_out_11), .out_12(reg8_1_out_12), .out_13(reg8_1_out_13), .out_14(reg8_1_out_14),
    .out_15(reg8_1_out_15), .out_16(reg8_1_out_16), .out_17(reg8_1_out_17));
  and and_1 (and_1_out, reg8_1_out_10, in_35);
  c8 c8_2 (
    .in_2(and_1_out), .in_3(reg8_1_out_11), .in_4(reg8_1_out_12), .in_5(reg8_1_out_13), .in_6(reg8_1_out_14),
    .in_7(reg8_1_out_15), .in_8(reg8_1_out_16), .in_9(reg8_1_out_17), .in_1(in_14), .out_10(out_37),
    .out_11(out_38), .out_12(out_39), .out_13(out_40), .out_14(out_41), .out_15(out_42), .out_16(out_43),
    .out_17(out_44));
endmodule

module reg8 (
  input  in_1,
  input  in_2,
  input  in_3,
  input  in_4,
  input  in_5,
  input  in_6,
  input  in_7,
  input  in_8,
  input  in_9,
  output out_10,
  output out_11,
  output out_12,
  output out_13,
  output out_14,
  output out_15,
  output out_16,
  output out_17
);

  Register register_1 (
    .D({in_1, in_2, in_3, in_4, in_5, in_6, in_7, in_9}),
    .Q({out_10, out_11, out_12, out_13, out_14, out_15, out_16, out_17}), .clk(in_8));  // open: en, clr
endmodule
