// Logisim project 实验.circ as structural Verilog: 18 circuits, main circuit main
module main (
  input  I0,
  input  I1,
  input  I2,
  input  I3,
  input  I4,
  input  I5,
  input  I6,
  input  I7,
  input  I8,
  input  I9,
  input  I10,
  input  I11,
  input  I12,
  input  I13,
  input  I14,
  input  I15,
  input  I0_2,
  input  I1_2,
  input  I2_2,
  input  I3_2,
  input  I4_2,
  input  I5_2,
  input  I6_2,
  input  I7_2,
  input  I8_2,
  input  I9_2,
  input  I10_2,
  input  I11_2,
  input  I12_2,
  input  I13_2,
  input  I14_2,
  input  I15_2,
  input  Wil,
  input  llen,
  output out_35
);

  wire c8_1_out_10, c8_1_out_11, c8_1_out_12, c8_1_out_13, c8_1_out_14, c8_1_out_15, c8_1_out_16,
       c8_1_out_17, clock_1_out, double_16key_1_out_37, double_16key_1_out_38, double_16key_1_out_39,
       double_16key_1_out_40, double_16key_1_out_41, double_16key_1_out_42, double_16key_1_out_43,
       double_16key_1_out_44, n2seg_1_out_10, n2seg_1_out_11, n2seg_1_out_12, n2seg_1_out_13, n2seg_1_out_14,
       n2seg_1_out_15, n2seg_1_out_16, n2seg_1_out_17, n2seg_1_out_18, n2seg_1_out_19, n2seg_1_out_20,
       n2seg_1_out_21, n2seg_1_out_22, n2seg_1_out_23, n8adder_1_s0, n8adder_1_s1, n8adder_1_s2,
       n8adder_1_s3, n8adder_1_s4, n8adder_1_s5, n8adder_1_s6, n8adder_1_s7, reg8_1_p1, reg8_1_p2, reg8_1_p3,
       reg8_1_p4, reg8_1_p5, reg8_1_p6, reg8_1_p7, reg8_1_p8, reg8_1_p9, reg8_1_p10, reg8_1_p11, reg8_1_p12,
       reg8_2_p13, reg8_2_p15, reg8_3_p1, reg8_3_p3, reg8_3_p6, reg8_3_p8, reg8_3_p10, reg8_3_p12,
       reg8_3_p14, reg8_3_p16, reg8_3_p18, reg8_3_p20;
  wire [3:0] counter_1_q;
  wire [8:0] rom_1_data;

  double_16key double_16key_1 (
    .I0(I0), .I1(I1), .I2(I2), .I3(I3), .I4(I4), .I5(I5), .I6(I6), .I7(I7), .I8(I8), .I9(I9), .I10(I10),
    .I11(I11), .I12(I12), .I13(I13), .I14(I14), .I15(I15), .I0_2(I0_2), .I1_2(I1_2), .I2_2(I2_2),
    .I3_2(I3_2), .I4_2(I4_2), .I5_2(I5_2), .I6_2(I6_2), .I7_2(I7_2), .I8_2(I8_2), .I9_2(I9_2), .I10_2(I10_2),
    .I11_2(I11_2), .I12_2(I12_2), .I13_2(I13_2), .I14_2(I14_2), .I15_2(I15_2),
    .out_37(double_16key_1_out_37), .out_38(double_16key_1_out_38), .out_39(double_16key_1_out_39),
    .out_40(double_16key_1_out_40), .out_41(double_16key_1_out_41), .out_42(double_16key_1_out_42),
    .out_43(double_16key_1_out_43), .out_44(double_16key_1_out_44), .in_12(rom_1_data[8]),
    .in_13(rom_1_data[7]), .in_33(Wil), .in_35(llen));
  LED led_1 (.in(double_16key_1_out_41));
  LED led_2 (.in(double_16key_1_out_37));
  LED led_3 (.in(double_16key_1_out_42));
  LED led_4 (.in(double_16key_1_out_38));
  LED led_5 (.in(double_16key_1_out_39));
  LED led_6 (.in(double_16key_1_out_40));
  LED led_7 (.in(double_16key_1_out_43));
  LED led_8 (.in(double_16key_1_out_44));
  C8 c8_1 (
    .in_2(double_16key_1_out_44), .in_3(double_16key_1_out_43), .in_4(double_16key_1_out_42),
    .in_5(double_16key_1_out_41), .in_6(double_16key_1_out_40), .in_7(double_16key_1_out_39),
    .in_8(double_16key_1_out_38), .in_9(double_16key_1_out_37), .out_10(c8_1_out_10), .out_11(c8_1_out_11),
    .out_12(c8_1_out_12), .out_13(c8_1_out_13), .out_14(c8_1_out_14), .out_15(c8_1_out_15),
    .out_16(c8_1_out_16), .out_17(c8_1_out_17), .in_1(rom_1_data[6]));
  C8 c8_2 (
    .in_2(n8adder_1_s0), .in_3(n8adder_1_s1), .in_4(n8adder_1_s2), .in_5(n8adder_1_s3), .in_6(n8adder_1_s4),
    .in_7(n8adder_1_s5), .in_8(n8adder_1_s6), .in_9(n8adder_1_s7), .out_10(c8_1_out_17),
    .out_11(c8_1_out_16), .out_12(c8_1_out_15), .out_13(c8_1_out_14), .out_14(c8_1_out_13),
    .out_15(c8_1_out_12), .out_16(c8_1_out_11), .out_17(c8_1_out_10), .in_1(rom_1_data[4]));
  C8 c8_3 (
    .in_2(reg8_2_p15), .in_3(reg8_2_p13), .in_4(reg8_1_p12), .in_5(reg8_1_p10), .in_6(reg8_1_p8),
    .in_7(reg8_1_p6), .in_8(reg8_1_p4), .in_9(reg8_1_p2), .out_10(double_16key_1_out_37),
    .out_11(double_16key_1_out_38), .out_12(double_16key_1_out_39), .out_13(double_16key_1_out_40),
    .out_14(double_16key_1_out_41), .out_15(double_16key_1_out_42), .out_16(double_16key_1_out_43),
    .out_17(double_16key_1_out_44), .in_1(rom_1_data[5]));
  _8adder u_8adder_1 (
    .B7(reg8_1_p1), .B6(reg8_1_p3), .B5(reg8_1_p5), .B4(reg8_1_p7), .B3(reg8_1_p9), .B2(reg8_1_p11),
    .B1(reg8_3_p1), .B0(reg8_3_p3), .A7(reg8_3_p6), .A6(reg8_3_p8), .A5(reg8_3_p10), .A4(reg8_3_p12),
    .A3(reg8_3_p14), .A2(reg8_3_p16), .A1(reg8_3_p18), .A0(reg8_3_p20), .C(out_35), .S7(n8adder_1_s7),
    .S6(n8adder_1_s6), .S5(n8adder_1_s5), .S4(n8adder_1_s4), .S3(n8adder_1_s3), .S2(n8adder_1_s2),
    .S1(n8adder_1_s1), .S0(n8adder_1_s0));
  // reg8 reg8_1: pin names not known; wires that end beside it: reg8_1_p1, reg8_1_p2, reg8_1_p3, reg8_1_p4, reg8_1_p5, reg8_1_p6, reg8_1_p7, reg8_1_p8, reg8_1_p9, reg8_1_p10, reg8_1_p11, reg8_1_p12
  // reg8 reg8_2: pin names not known; wires that end beside it: reg8_1_p2, c8_1_out_17, reg8_1_p4, c8_1_out_16, reg8_1_p6, c8_1_out_15, reg8_1_p8, c8_1_out_14, reg8_1_p10, c8_1_out_13, reg8_1_p12, c8_1_out_12, reg8_2_p13, c8_1_out_11, reg8_2_p15, c8_1_out_10, rom_1_data[3]
  // reg8 reg8_3: pin names not known; wires that end beside it: reg8_3_p1, reg8_2_p13, reg8_3_p3, reg8_2_p15, rom_1_data[2], reg8_3_p6, reg8_1_p2, reg8_3_p8, reg8_1_p4, reg8_3_p10, reg8_1_p6, reg8_3_p12, reg8_1_p8, reg8_3_p14, reg8_1_p10, reg8_3_p16, reg8_1_p12, reg8_3_p18, reg8_2_p13, reg8_3_p20, reg8_2_p15, rom_1_data[1]
  Clock clock_1 (.out(clock_1_out));
  Counter #(.width(4), .max('hf)) counter_1 (.Q(counter_1_q), .clk(clock_1_out));  // open: load, D, count, carry, clr
  _2seg u_2seg_1 (
    .in_2(double_16key_1_out_37), .in_3(double_16key_1_out_38), .in_4(double_16key_1_out_39),
    .in_5(double_16key_1_out_40), .in_6(double_16key_1_out_41), .in_7(double_16key_1_out_42),
    .in_8(double_16key_1_out_43), .in_9(double_16key_1_out_44), .out_10(n2seg_1_out_10),
    .out_11(n2seg_1_out_11), .out_12(n2seg_1_out_12), .out_13(n2seg_1_out_13), .out_14(n2seg_1_out_14),
    .out_15(n2seg_1_out_15), .out_16(n2seg_1_out_16), .out_17(n2seg_1_out_17), .out_18(n2seg_1_out_18),
    .out_19(n2seg_1_out_19), .out_20(n2seg_1_out_20), .out_21(n2seg_1_out_21), .out_22(n2seg_1_out_22),
    .out_23(n2seg_1_out_23), .in_1(rom_1_data[0]));
  _7_Segment_Display #(.active("false")) u_7_segment_display_1 (
    .g(n2seg_1_out_16), .f(n2seg_1_out_15), .a(n2seg_1_out_10), .b(n2seg_1_out_11), .e(n2seg_1_out_14),
    .d(n2seg_1_out_13), .c(n2seg_1_out_12), .dp(1'b1));
  ROM #(.addrWidth(4), .dataWidth(9)) rom_1 (.addr(counter_1_q), .data(rom_1_data));  // open: sel
  _7_Segment_Display #(.active("false")) u_7_segment_display_2 (
    .g(n2seg_1_out_23), .f(n2seg_1_out_22), .a(n2seg_1_out_17), .b(n2seg_1_out_18), .e(n2seg_1_out_21),
    .d(n2seg_1_out_20), .c(n2seg_1_out_19), .dp(1'b1));

  // Notes on the sheet:
  //   I0
  //   contents of rom_1 (hex, n*v repeats v):
  //   141 149 141 3 1 81 c1 c9 c1 5 11 19 11 21
endmodule

module a (
  input  D3,
  input  D2,
  input  D1,
  input  D0,
  output A
);

  wire not_1_out, not_2_out, not_3_out, not_4_out, x1_out, x2_out, x3_out, x4_out;

  not not_1 (not_1_out, D3);
  not not_2 (not_2_out, D2);
  not not_3 (not_3_out, D1);
  not not_4 (not_4_out, D0);
  and x1 (x1_out, not_1_out, not_2_out, not_3_out, D0);
  and x2 (x2_out, not_1_out, D2, not_3_out, not_4_out);
  and x3 (x3_out, D3, not_2_out, D1, D0);
  and x4 (x4_out, D3, D2, not_3_out, D0);
  or or_1 (A, x1_out, x2_out, x3_out, x4_out);
endmodule

module b (
  input  D3,
  input  D2,
  input  D1,
  input  D0,
  output B
);

  wire not_1_out, not_2_out, not_3_out, not_4_out, x1_out, x2_out, x3_out, x4_out, x5_out, x6_out;

  not not_1 (not_1_out, D3);
  not not_2 (not_2_out, D2);
  not not_3 (not_3_out, D1);
  not not_4 (not_4_out, D0);
  and x1 (x1_out, not_1_out, D2, not_3_out, D0);
  and x2 (x2_out, not_1_out, D2, D1, not_4_out);
  and x3 (x3_out, D3, not_2_out, D1, D0);
  and x4 (x4_out, D3, D2, not_3_out, not_4_out);
  and x5 (x5_out, D3, D2, D1, not_4_out);
  and x6 (x6_out, D3, D2, D1, D0);
  or or_1 (B, x1_out, x2_out, x3_out, x4_out, x5_out, x6_out);
endmodule

module c (
  input  D3,
  input  D2,
  input  D1,
  input  D0,
  output C
);

  wire not_1_out, not_2_out, not_3_out, not_4_out, x1_out, x2_out, x3_out, x4_out;

  not not_1 (not_1_out, D3);
  not not_2 (not_2_out, D2);
  not not_3 (not_3_out, D1);
  not not_4 (not_4_out, D0);
  and x1 (x1_out, not_1_out, not_2_out, D1, not_4_out);
  and x2 (x2_out, D3, D2, not_3_out, not_4_out);
  and x3 (x3_out, D3, D2, D1, not_4_out);
  and x4 (x4_out, D3, D2, D1, D0);
  or or_1 (C, x1_out, x2_out, x3_out, x4_out);
endmodule

module d (
  input  D3,
  input  D2,
  input  D1,
  input  D0,
  output D
);

  wire not_1_out, not_2_out, not_3_out, not_4_out, x1_out, x2_out, x3_out, x4_out, x5_out;

  not not_1 (not_1_out, D3);
  not not_2 (not_2_out, D2);
  not not_3 (not_3_out, D1);
  not not_4 (not_4_out, D0);
  and x1 (x1_out, not_1_out, not_2_out, not_3_out, D0);
  and x2 (x2_out, not_1_out, D2, not_3_out, not_4_out);
  and x3 (x3_out, not_1_out, D2, D1, D0);
  and x4 (x4_out, D3, not_2_out, D1, not_4_out);
  and x5 (x5_out, D3, D2, D1, D0);
  or or_1 (D, x1_out, x2_out, x3_out, x4_out, x5_out);
endmodule

module e (
  input  D3,
  input  D2,
  input  D1,
  input  D0,
  output E
);

  wire not_1_out, not_2_out, not_3_out, not_4_out, x1_out, x2_out, x3_out, x4_out, x5_out, x6_out;

  not not_1 (not_1_out, D3);
  not not_2 (not_2_out, D2);
  not not_3 (not_3_out, D1);
  not not_4 (not_4_out, D0);
  and x1 (x1_out, not_1_out, not_2_out, not_3_out, D0);
  and x2 (x2_out, not_1_out, not_2_out, D1, D0);
  and x3 (x3_out, not_1_out, D2, not_3_out, not_4_out);
  and x4 (x4_out, not_1_out, D2, not_3_out, D0);
  and x5 (x5_out, not_1_out, D2, D1, D0);
  and x6 (x6_out, D3, not_2_out, not_3_out, D0);
  or or_1 (E, x1_out, x2_out, x3_out, x4_out, x5_out, x6_out);
endmodule

module f (
  input  D3,
  input  D2,
  input  D1,
  input  D0,
  output F
);

  wire not_1_out, not_2_out, not_3_out, not_4_out, x1_out, x2_out, x3_out, x4_out, x5_out;

  not not_1 (not_1_out, D3);
  not not_2 (not_2_out, D2);
  not not_3 (not_3_out, D1);
  not not_4 (not_4_out, D0);
  and x1 (x1_out, not_1_out, not_2_out, not_3_out, D0);
  and x2 (x2_out, not_1_out, not_2_out, D1, not_4_out);
  and x3 (x3_out, not_1_out, not_2_out, D1, D0);
  and x4 (x4_out, not_1_out, D2, D1, D0);
  and x5 (x5_out, D3, D2, not_3_out, D0);
  or or_1 (F, x1_out, x2_out, x3_out, x4_out, x5_out);
endmodule

module g (
  input  D3,
  input  D2,
  input  D1,
  input  D0,
  output G
);

  wire not_1_out, not_2_out, not_3_out, not_4_out, x1_out, x2_out, x3_out, x4_out;

  not not_1 (not_1_out, D3);
  not not_2 (not_2_out, D2);
  not not_3 (not_3_out, D1);
  not not_4 (not_4_out, D0);
  and x1 (x1_out, not_1_out, not_2_out, not_3_out, not_4_out);
  and x2 (x2_out, not_1_out, not_2_out, not_3_out, D0);
  and x3 (x3_out, not_1_out, D2, D1, D0);
  and x4 (x4_out, D3, D2, not_3_out, not_4_out);
  or or_1 (G, x1_out, x2_out, x3_out, x4_out);
endmodule

module \seg总  (
  input  in_1,
  input  in_2,
  input  in_3,
  input  in_4,
  output out_5,
  output out_6,
  output out_7,
  output out_8,
  output out_9,
  output out_10,
  output out_11
);

  a a_1 (.D3(in_1), .D2(in_2), .D1(in_3), .D0(in_4), .A(out_5));
  b b_1 (.D3(in_1), .D2(in_2), .D1(in_3), .D0(in_4), .B(out_6));
  c c_1 (.D3(in_1), .D2(in_2), .D1(in_3), .D0(in_4), .C(out_7));
  d d_1 (.D3(in_1), .D2(in_2), .D1(in_3), .D0(in_4), .D(out_8));
  e e_1 (.D3(in_1), .D2(in_2), .D1(in_3), .D0(in_4), .E(out_9));
  f f_1 (.D3(in_1), .D2(in_2), .D1(in_3), .D0(in_4), .F(out_10));
  g g_1 (.D3(in_1), .D2(in_2), .D1(in_3), .D0(in_4), .G(out_11));
endmodule

module seg_test (
  input  I3,
  input  I2,
  input  I1,
  input  I0
);

  wire \seg总_1_out_5 , \seg总_1_out_6 , \seg总_1_out_7 , \seg总_1_out_8 , \seg总_1_out_9 , \seg总_1_out_10 ,
       \seg总_1_out_11 ;

  \seg总  \seg总_1  (
    .in_1(I3), .in_2(I2), .in_3(I1), .in_4(I0), .out_5(\seg总_1_out_5 ), .out_6(\seg总_1_out_6 ),
    .out_7(\seg总_1_out_7 ), .out_8(\seg总_1_out_8 ), .out_9(\seg总_1_out_9 ), .out_10(\seg总_1_out_10 ),
    .out_11(\seg总_1_out_11 ));
  _7_Segment_Display #(.active("false")) u_7_segment_display_1 (
    .g(\seg总_1_out_11 ), .f(\seg总_1_out_10 ), .a(\seg总_1_out_5 ), .b(\seg总_1_out_6 ), .e(\seg总_1_out_9 ),
    .d(\seg总_1_out_8 ), .c(\seg总_1_out_7 ), .dp(1'b1));
endmodule

module C8 (
  input  in_1,
  input  in_2,
  input  in_3,
  input  in_4,
  input  in_5,
  input  in_6,
  input  in_7,
  input  in_8,
  input  in_9,
  output out_10,
  output out_11,
  output out_12,
  output out_13,
  output out_14,
  output out_15,
  output out_16,
  output out_17
);

  assign out_10 = in_1 ? in_2 : 1'bz;  // Controlled_Buffer controlled_buffer_1
  assign out_11 = in_1 ? in_3 : 1'bz;  // Controlled_Buffer controlled_buffer_2
  assign out_12 = in_1 ? in_4 : 1'bz;  // Controlled_Buffer controlled_buffer_3
  assign out_13 = in_1 ? in_5 : 1'bz;  // Controlled_Buffer controlled_buffer_4
  assign out_14 = in_1 ? in_6 : 1'bz;  // Controlled_Buffer controlled_buffer_5
  assign out_15 = in_1 ? in_7 : 1'bz;  // Controlled_Buffer controlled_buffer_6
  assign out_16 = in_1 ? in_8 : 1'bz;  // Controlled_Buffer controlled_buffer_7
  assign out_17 = in_1 ? in_9 : 1'bz;  // Controlled_Buffer controlled_buffer_8
endmodule

module _16_4 (
  input  I0,
  input  I1,
  input  I2,
  input  I3,
  input  I4,
  input  I5,
  input  I6,
  input  I7,
  input  I8,
  input  I9,
  input  I10,
  input  I11,
  input  I12,
  input  I13,
  input  I14,
  input  I15,
  output Y3,
  output Y2,
  output Y1,
  output Y0
);

  or or_1 (Y0, I1, I3, I5, I7, I9, I11, I13, I15);
  or or_2 (Y1, I2, I3, I6, I7, I10, I11, I14, I15);
  or or_3 (Y2, I4, I5, I7, I6, I12, I13, I14, I15);
  or or_4 (Y3, I8, I9, I11, I10, I12, I13, I14, I15);
endmodule

module _16key (
  input  I0,
  input  I1,
  input  I2,
  input  in_4,
  input  I3,
  input  I4,
  input  I5,
  input  I6,
  input  I7,
  input  I8,
  input  I9,
  input  I10,
  input  I11,
  input  I12,
  input  I13,
  input  I14,
  input  I15,
  input  I0_2,
  input  I1_2,
  input  I2_2,
  input  I3_2,
  input  I4_2,
  input  I5_2,
  input  I6_2,
  input  I7_2,
  input  I8_2,
  input  I9_2,
  input  I10_2,
  input  I11_2,
  input  I12_2,
  input  I13_2,
  input  I14_2,
  input  I15_2,
  output out_34,
  output out_35,
  output out_36,
  output out_37,
  output out_38,
  output out_39,
  output out_40,
  output out_41
);

  wire n16_4_1_y0, n16_4_1_y1, n16_4_1_y2, n16_4_1_y3, n16_4_2_y0, n16_4_2_y1, n16_4_2_y2, n16_4_2_y3;

  _16_4 u_16_4_1 (
    .I0(I0), .I1(I1), .I2(I2), .I3(I3), .I4(I4), .I5(I5), .I6(I6), .I7(I7), .I8(I8), .I9(I9), .I10(I10),
    .I11(I11), .I12(I12), .I13(I13), .I14(I14), .I15(I15), .Y0(n16_4_1_y0), .Y1(n16_4_1_y1), .Y2(n16_4_1_y2),
    .Y3(n16_4_1_y3));
  _16_4 u_16_4_2 (
    .I0(I0_2), .I1(I1_2), .I2(I2_2), .I3(I3_2), .I4(I4_2), .I5(I5_2), .I6(I6_2), .I7(I7_2), .I8(I8_2),
    .I9(I9_2), .I10(I10_2), .I11(I11_2), .I12(I12_2), .I13(I13_2), .I14(I14_2), .I15(I15_2), .Y0(n16_4_2_y0),
    .Y1(n16_4_2_y1), .Y2(n16_4_2_y2), .Y3(n16_4_2_y3));
  C8 c8_1 (
    .in_2(n16_4_1_y3), .in_3(n16_4_1_y2), .in_4(n16_4_1_y1), .in_5(n16_4_1_y0), .in_6(n16_4_2_y3),
    .in_7(n16_4_2_y2), .in_8(n16_4_2_y1), .in_9(n16_4_2_y0), .out_10(out_34), .out_11(out_35),
    .out_12(out_36), .out_13(out_37), .out_14(out_38), .out_15(out_39), .out_16(out_40), .out_17(out_41),
    .in_1(in_4));
endmodule

module double_16key (
  input  I0,
  input  I1,
  input  I2,
  input  I3,
  input  I4,
  input  I5,
  input  I6,
  input  I7,
  input  I8,
  input  I9,
  input  I10,
  input  in_12,
  input  in_13,
  input  I11,
  input  I12,
  input  I13,
  input  I14,
  input  I15,
  input  I0_2,
  input  I1_2,
  input  I2_2,
  input  I3_2,
  input  I4_2,
  input  I5_2,
  input  I6_2,
  input  I7_2,
  input  I8_2,
  input  I9_2,
  input  I10_2,
  input  I11_2,
  input  I12_2,
  input  I13_2,
  input  in_33,
  input  I14_2,
  input  in_35,
  input  I15_2,
  output out_37,
  output out_38,
  output out_39,
  output out_40,
  output out_41,
  output out_42,
  output out_43,
  output out_44
);

  wire and_1_out, n16_4_1_y0, n16_4_1_y1, n16_4_1_y2, n16_4_1_y3, n16_4_2_y0, n16_4_2_y1, n16_4_2_y2,
       n16_4_2_y3, reg8_1_p10, reg8_1_p11, reg8_1_p12, reg8_1_p13, reg8_1_p14, reg8_1_p15, reg8_1_p16,
       reg8_1_p17;

  _16_4 u_16_4_1 (
    .I0(I0), .I1(I1), .I2(I2), .I3(I3), .I4(I4), .I5(I5), .I6(I6), .I7(I7), .I8(I8), .I9(I9), .I10(I10),
    .I11(I11), .I12(I12), .I13(I13), .I14(I14), .I15(I15), .Y0(n16_4_1_y0), .Y1(n16_4_1_y1), .Y2(n16_4_1_y2),
    .Y3(n16_4_1_y3));
  _16_4 u_16_4_2 (
    .I0(I0_2), .I1(I1_2), .I2(I2_2), .I3(I3_2), .I4(I4_2), .I5(I5_2), .I6(I6_2), .I7(I7_2), .I8(I8_2),
    .I9(I9_2), .I10(I10_2), .I11(I11_2), .I12(I12_2), .I13(I13_2), .I14(I14_2), .I15(I15_2), .Y0(n16_4_2_y0),
    .Y1(n16_4_2_y1), .Y2(n16_4_2_y2), .Y3(n16_4_2_y3));
  C8 c8_1 (
    .in_2(n16_4_1_y3), .in_3(n16_4_1_y2), .in_4(n16_4_1_y1), .in_5(n16_4_1_y0), .in_6(n16_4_2_y3),
    .in_7(n16_4_2_y2), .in_8(n16_4_2_y1), .in_9(n16_4_2_y0), .out_10(out_37), .out_11(out_38),
    .out_12(out_39), .out_13(out_40), .out_14(out_41), .out_15(out_42), .out_16(out_43), .out_17(out_44),
    .in_1(in_12));
  // reg8 reg8_1: pin names not known; wires that end beside it: n16_4_1_y3, n16_4_1_y2, n16_4_1_y1, n16_4_1_y0, n16_4_2_y3, n16_4_2_y2, n16_4_2_y1, n16_4_2_y0, in_33, reg8_1_p10, reg8_1_p11, reg8_1_p12, reg8_1_p13, reg8_1_p14, reg8_1_p15, reg8_1_p16, reg8_1_p17
  and and_1 (and_1_out, reg8_1_p10, in_35);
  C8 c8_2 (
    .in_2(and_1_out), .in_3(reg8_1_p11), .in_4(reg8_1_p12), .in_5(reg8_1_p13), .in_6(reg8_1_p14),
    .in_7(reg8_1_p15), .in_8(reg8_1_p16), .in_9(reg8_1_p17), .out_10(out_37), .out_11(out_38),
    .out_12(out_39), .out_13(out_40), .out_14(out_41), .out_15(out_42), .out_16(out_43), .out_17(out_44),
    .in_1(in_13));
endmodule

module _2seg (
  input  in_1,
  input  in_2,
  input  in_3,
  input  in_4,
  input  in_5,
  input  in_6,
  input  in_7,
  input  in_8,
  input  in_9,
  output out_10,
  output out_11,
  output out_12,
  output out_13,
  output out_14,
  output out_15,
  output out_16,
  output out_17,
  output out_18,
  output out_19,
  output out_20,
  output out_21,
  output out_22,
  output out_23
);

  wire c8_1_out_10, c8_1_out_11, c8_1_out_12, c8_1_out_13, c8_1_out_14, c8_1_out_15, c8_1_out_16, c8_1_out_17;

  C8 c8_1 (
    .in_2(in_2), .in_3(in_3), .in_4(in_4), .in_5(in_5), .in_6(in_6), .in_7(in_7), .in_8(in_8), .in_9(in_9),
    .out_10(c8_1_out_10), .out_11(c8_1_out_11), .out_12(c8_1_out_12), .out_13(c8_1_out_13),
    .out_14(c8_1_out_14), .out_15(c8_1_out_15), .out_16(c8_1_out_16), .out_17(c8_1_out_17), .in_1(in_1));
  \seg总  \seg总_1  (
    .in_1(c8_1_out_10), .in_2(c8_1_out_11), .in_3(c8_1_out_12), .in_4(c8_1_out_13), .out_5(out_10),
    .out_6(out_11), .out_7(out_12), .out_8(out_13), .out_9(out_14), .out_10(out_15), .out_11(out_16));
  \seg总  \seg总_2  (
    .in_1(c8_1_out_14), .in_2(c8_1_out_15), .in_3(c8_1_out_16), .in_4(c8_1_out_17), .out_5(out_17),
    .out_6(out_18), .out_7(out_19), .out_8(out_20), .out_9(out_21), .out_10(out_22), .out_11(out_23));
endmodule

module ha (
  input  A,
  input  B,
  output S,
  output C
);

  wire and_1_out, and_2_out, not_1_out, not_2_out;

  not not_1 (not_1_out, A);
  not not_2 (not_2_out, B);
  and and_1 (and_1_out, not_1_out, B);
  and and_2 (and_2_out, A, not_2_out);
  and and_3 (C, A, B);
  or or_1 (S, and_1_out, and_2_out);
endmodule

module FA (
  input  Cin,
  input  B,
  input  A,
  output Sum,
  output Cout
);

  wire ha_1_c, ha_1_s, ha_2_c;

  ha ha_1 (.A(B), .B(A), .S(ha_1_s), .C(ha_1_c));
  ha ha_2 (.A(Cin), .B(ha_1_s), .S(Sum), .C(ha_2_c));
  or or_1 (Cout, ha_2_c, ha_1_c);
endmodule

module _8adder (
  input  B7,
  input  B6,
  input  B5,
  input  B4,
  input  B3,
  input  B2,
  input  B1,
  input  B0,
  input  A7,
  input  A6,
  input  A5,
  input  A4,
  input  A3,
  input  A2,
  input  A1,
  input  A0,
  output C,
  output S7,
  output S6,
  output S5,
  output S4,
  output S3,
  output S2,
  output S1,
  output S0
);

  wire fa_1_cout, fa_2_cout, fa_3_cout, fa_4_cout, fa_5_cout, fa_6_cout, fa_7_cout;

  FA fa_1 (.Cin(1'b0), .B(B0), .A(A0), .Sum(S0), .Cout(fa_1_cout));
  FA fa_2 (.Cin(fa_3_cout), .B(B2), .A(A2), .Sum(S2), .Cout(fa_2_cout));
  FA fa_3 (.Cin(fa_1_cout), .B(B1), .A(A1), .Sum(S1), .Cout(fa_3_cout));
  FA fa_4 (.Cin(fa_2_cout), .B(B3), .A(A3), .Sum(S3), .Cout(fa_4_cout));
  FA fa_5 (.Cin(fa_6_cout), .B(B5), .A(A5), .Sum(S5), .Cout(fa_5_cout));
  FA fa_6 (.Cin(fa_4_cout), .B(B4), .A(A4), .Sum(S4), .Cout(fa_6_cout));
  FA fa_7 (.Cin(fa_5_cout), .B(B6), .A(A6), .Sum(S6), .Cout(fa_7_cout));
  FA fa_8 (.Cin(fa_7_cout), .B(B7), .A(A7), .Sum(S7), .Cout(C));
endmodule
