// Logisim project 实验三多端口输入设计.circ as structural Verilog: 16 circuits, main circuit main
module main (
  input  I0,
  input  I1,
  input  in_3,
  input  in_4,
  input  I2,
  input  I3,
  input  I4,
  input  I5,
  input  I6,
  input  I7,
  input  I8,
  input  I9,
  input  I10,
  input  I11,
  input  in_15,
  input  I12,
  input  I13,
  input  I14,
  input  I15,
  input  I0_2,
  input  I1_2,
  input  I2_2,
  input  in_23,
  input  in_24,
  input  I3_2,
  input  I4_2,
  input  I5_2,
  input  I6_2,
  input  I7_2,
  input  I8_2,
  input  I9_2,
  input  I10_2,
  input  I11_2,
  input  I12_2,
  input  I13_2,
  input  I14_2,
  input  I15_2
);

  wire double_16key_1_out_37, double_16key_1_out_38, double_16key_1_out_39, double_16key_1_out_40,
       double_16key_1_out_41, double_16key_1_out_42, double_16key_1_out_43, double_16key_1_out_44,
       n2seg_1_out_10, n2seg_1_out_11, n2seg_1_out_12, n2seg_1_out_13, n2seg_1_out_14, n2seg_1_out_15,
       n2seg_1_out_16, n2seg_1_out_17, n2seg_1_out_18, n2seg_1_out_19, n2seg_1_out_20, n2seg_1_out_21,
       n2seg_1_out_22, n2seg_1_out_23;

  double_16key double_16key_1 (
    .I0(I0), .I1(I1), .I2(I2), .I3(I3), .I4(I4), .I5(I5), .I6(I6), .I7(I7), .I8(I8), .I9(I9), .I10(I10),
    .I11(I11), .I12(I12), .I13(I13), .I14(I14), .I15(I15), .I0_2(I0_2), .I1_2(I1_2), .I2_2(I2_2),
    .I3_2(I3_2), .I4_2(I4_2), .I5_2(I5_2), .I6_2(I6_2), .I7_2(I7_2), .I8_2(I8_2), .I9_2(I9_2), .I10_2(I10_2),
    .I11_2(I11_2), .I12_2(I12_2), .I13_2(I13_2), .I14_2(I14_2), .I15_2(I15_2), .in_13(in_3), .in_14(in_4),
    .in_34(in_23), .in_35(in_24), .out_37(double_16key_1_out_37), .out_38(double_16key_1_out_38),
    .out_39(double_16key_1_out_39), .out_40(double_16key_1_out_40), .out_41(double_16key_1_out_41),
    .out_42(double_16key_1_out_42), .out_43(double_16key_1_out_43), .out_44(double_16key_1_out_44));
  LED led_1 (.in(double_16key_1_out_37));
  LED led_2 (.in(double_16key_1_out_41));
  LED led_3 (.in(double_16key_1_out_38));
  LED led_4 (.in(double_16key_1_out_42));
  LED led_5 (.in(double_16key_1_out_39));
  LED led_6 (.in(double_16key_1_out_40));
  LED led_7 (.in(double_16key_1_out_43));
  LED led_8 (.in(double_16key_1_out_44));
  _2seg u_2seg_1 (
    .in_1(double_16key_1_out_37), .in_3(double_16key_1_out_38), .in_4(double_16key_1_out_39),
    .in_5(double_16key_1_out_40), .in_6(double_16key_1_out_41), .in_7(double_16key_1_out_42),
    .in_8(double_16key_1_out_43), .in_9(double_16key_1_out_44), .in_2(in_15), .out_10(n2seg_1_out_10),
    .out_11(n2seg_1_out_11), .out_12(n2seg_1_out_12), .out_13(n2seg_1_out_13), .out_14(n2seg_1_out_14),
    .out_15(n2seg_1_out_15), .out_16(n2seg_1_out_16), .out_17(n2seg_1_out_17), .out_18(n2seg_1_out_18),
    .out_19(n2seg_1_out_19), .out_20(n2seg_1_out_20), .out_21(n2seg_1_out_21), .out_22(n2seg_1_out_22),
    .out_23(n2seg_1_out_23));
  _7_Segment_Display #(.active("false")) u_7_segment_display_1 (
    .g(n2seg_1_out_16), .f(n2seg_1_out_15), .a(n2seg_1_out_10), .b(n2seg_1_out_11), .e(n2seg_1_out_14),
    .d(n2seg_1_out_13), .c(n2seg_1_out_12), .dp(1'b1));
  _7_Segment_Display #(.active("false")) u_7_segment_display_2 (
    .g(n2seg_1_out_23), .f(n2seg_1_out_22), .a(n2seg_1_out_17), .b(n2seg_1_out_18), .e(n2seg_1_out_21),
    .d(n2seg_1_out_20), .c(n2seg_1_out_19), .dp(1'b1));
endmodule

module Seg_A (
  input  D3,
  input  D2,
  input  D1,
  input  D0,
  output A
);

  wire not_1_out, not_2_out, not_3_out, not_4_out, x1_out, x2_out, x3_out, x4_out;

  not not_1 (not_1_out, D3);
  not not_2 (not_2_out, D2);
  not not_3 (not_3_out, D1);
  not not_4 (not_4_out, D0);
  and x1 (x1_out, not_1_out, not_2_out, not_3_out, D0);
  and x2 (x2_out, not_1_out, D2, not_3_out, not_4_out);
  and x3 (x3_out, D3, not_2_out, D1, D0);
  and x4 (x4_out, D3, D2, not_3_out, D0);
  or or_1 (A, x1_out, x2_out, x3_out, x4_out);
endmodule

module Seg_B (
  input  D3,
  input  D2,
  input  D1,
  input  D0,
  output B
);

  wire not_1_out, not_2_out, not_3_out, not_4_out, x1_out, x2_out, x3_out, x4_out, x5_out, x6_out;

  not not_1 (not_1_out, D3);
  not not_2 (not_2_out, D2);
  not not_3 (not_3_out, D1);
  not not_4 (not_4_out, D0);
  and x1 (x1_out, not_1_out, D2, not_3_out, D0);
  and x2 (x2_out, not_1_out, D2, D1, not_4_out);
  and x3 (x3_out, D3, not_2_out, D1, D0);
  and x4 (x4_out, D3, D2, not_3_out, not_4_out);
  and x5 (x5_out, D3, D2, D1, not_4_out);
  and x6 (x6_out, D3, D2, D1, D0);
  or or_1 (B, x1_out, x2_out, x3_out, x4_out, x5_out, x6_out);
endmodule

module Seg_C (
  input  D3,
  input  D2,
  input  D1,
  input  D0,
  output C
);

  wire not_1_out, not_2_out, not_3_out, not_4_out, x1_out, x2_out, x3_out, x4_out;

  not not_1 (not_1_out, D3);
  not not_2 (not_2_out, D2);
  not not_3 (not_3_out, D1);
  not not_4 (not_4_out, D0);
  and x1 (x1_out, not_1_out, not_2_out, D1, not_4_out);
  and x2 (x2_out, D3, D2, not_3_out, not_4_out);
  and x3 (x3_out, D3, D2, D1, not_4_out);
  and x4 (x4_out, D3, D2, D1, D0);
  or or_1 (C, x1_out, x2_out, x3_out, x4_out);
endmodule

module Seg_D (
  input  D3,
  input  D2,
  input  D1,
  input  D0,
  output D
);

  wire not_1_out, not_2_out, not_3_out, not_4_out, x1_out, x2_out, x3_out, x4_out, x5_out;

  not not_1 (not_1_out, D3);
  not not_2 (not_2_out, D2);
  not not_3 (not_3_out, D1);
  not not_4 (not_4_out, D0);
  and x1 (x1_out, not_1_out, not_2_out, not_3_out, D0);
  and x2 (x2_out, not_1_out, D2, not_3_out, not_4_out);
  and x3 (x3_out, not_1_out, D2, D1, D0);
  and x4 (x4_out, D3, not_2_out, D1, not_4_out);
  and x5 (x5_out, D3, D2, D1, D0);
  or or_1 (D, x1_out, x2_out, x3_out, x4_out, x5_out);
endmodule

module Seg_E (
  input  D3,
  input  D2,
  input  D1,
  input  D0,
  output E
);

  wire not_1_out, not_2_out, not_3_out, not_4_out, x1_out, x2_out, x3_out, x4_out, x5_out, x6_out;

  not not_1 (not_1_out, D3);
  not not_2 (not_2_out, D2);
  not not_3 (not_3_out, D1);
  not not_4 (not_4_out, D0);
  and x1 (x1_out, not_1_out, not_2_out, not_3_out, D0);
  and x2 (x2_out, not_1_out, not_2_out, D1, D0);
  and x3 (x3_out, not_1_out, D2, not_3_out, not_4_out);
  and x4 (x4_out, not_1_out, D2, not_3_out, D0);
  and x5 (x5_out, not_1_out, D2, D1, D0);
  and x6 (x6_out, D3, not_2_out, not_3_out, D0);
  or or_1 (E, x1_out, x2_out, x3_out, x4_out, x5_out, x6_out);
endmodule

module Seg_F (
  input  D3,
  input  D2,
  input  D1,
  input  D0,
  output F
);

  wire not_1_out, not_2_out, not_3_out, not_4_out, x1_out, x2_out, x3_out, x4_out, x5_out;

  not not_1 (not_1_out, D3);
  not not_2 (not_2_out, D2);
  not not_3 (not_3_out, D1);
  not not_4 (not_4_out, D0);
  and x1 (x1_out, not_1_out, not_2_out, not_3_out, D0);
  and x2 (x2_out, not_1_out, not_2_out, D1, not_4_out);
  and x3 (x3_out, not_1_out, not_2_out, D1, D0);
  and x4 (x4_out, not_1_out, D2, D1, D0);
  and x5 (x5_out, D3, D2, not_3_out, D0);
  or or_1 (F, x1_out, x2_out, x3_out, x4_out, x5_out);
endmodule

module Seg_G (
  input  D3,
  input  D2,
  input  D1,
  input  D0,
  output G
);

  wire not_1_out, not_2_out, not_3_out, not_4_out, x1_out, x2_out, x3_out, x4_out;

  not not_1 (not_1_out, D3);
  not not_2 (not_2_out, D2);
  not not_3 (not_3_out, D1);
  not not_4 (not_4_out, D0);
  and x1 (x1_out, not_1_out, not_2_out, not_3_out, not_4_out);
  and x2 (x2_out, not_1_out, not_2_out, not_3_out, D0);
  and x3 (x3_out, not_1_out, D2, D1, D0);
  and x4 (x4_out, D3, D2, not_3_out, not_4_out);
  or or_1 (G, x1_out, x2_out, x3_out, x4_out);
endmodule

module Seg (
  input  in_1,
  input  in_2,
  input  in_3,
  input  in_4,
  output out_5,
  output out_6,
  output out_7,
  output out_8,
  output out_9,
  output out_10,
  output out_11
);

  Seg_A seg_a_1 (.D3(in_1), .D2(in_2), .D1(in_3), .D0(in_4), .A(out_5));
  Seg_B seg_b_1 (.D3(in_1), .D2(in_2), .D1(in_3), .D0(in_4), .B(out_6));
  Seg_C seg_c_1 (.D3(in_1), .D2(in_2), .D1(in_3), .D0(in_4), .C(out_7));
  Seg_D seg_d_1 (.D3(in_1), .D2(in_2), .D1(in_3), .D0(in_4), .D(out_8));
  Seg_E seg_e_1 (.D3(in_1), .D2(in_2), .D1(in_3), .D0(in_4), .E(out_9));
  Seg_F seg_f_1 (.D3(in_1), .D2(in_2), .D1(in_3), .D0(in_4), .F(out_10));
  Seg_G seg_g_1 (.D3(in_1), .D2(in_2), .D1(in_3), .D0(in_4), .G(out_11));
endmodule

module Seg_Example (
  input  in_1,
  input  in_2,
  input  in_3,
  input  in_4
);

  wire seg_1_out_5, seg_1_out_6, seg_1_out_7, seg_1_out_8, seg_1_out_9, seg_1_out_10, seg_1_out_11;

  Seg seg_1 (
    .in_1(in_1), .in_2(in_2), .in_3(in_3), .in_4(in_4), .out_5(seg_1_out_5), .out_6(seg_1_out_6),
    .out_7(seg_1_out_7), .out_8(seg_1_out_8), .out_9(seg_1_out_9), .out_10(seg_1_out_10),
    .out_11(seg_1_out_11));
  _7_Segment_Display #(.active("false")) u_7_segment_display_1 (
    .g(seg_1_out_11), .f(seg_1_out_10), .a(seg_1_out_5), .b(seg_1_out_6), .e(seg_1_out_9), .d(seg_1_out_8),
    .c(seg_1_out_7), .dp(1'b1));
endmodule

module C8 (
  input  in_1,
  input  in_2,
  input  in_3,
  input  in_4,
  input  in_5,
  input  in_6,
  input  in_7,
  input  in_8,
  input  in_9,
  output out_10,
  output out_11,
  output out_12,
  output out_13,
  output out_14,
  output out_15,
  output out_16,
  output out_17
);

  assign out_10 = in_1 ? in_2 : 1'bz;  // Controlled_Buffer controlled_buffer_1
  assign out_11 = in_1 ? in_3 : 1'bz;  // Controlled_Buffer controlled_buffer_2
  assign out_12 = in_1 ? in_4 : 1'bz;  // Controlled_Buffer controlled_buffer_3
  assign out_13 = in_1 ? in_5 : 1'bz;  // Controlled_Buffer controlled_buffer_4
  assign out_14 = in_1 ? in_6 : 1'bz;  // Controlled_Buffer controlled_buffer_5
  assign out_15 = in_1 ? in_7 : 1'bz;  // Controlled_Buffer controlled_buffer_6
  assign out_16 = in_1 ? in_8 : 1'bz;  // Controlled_Buffer controlled_buffer_7
  assign out_17 = in_1 ? in_9 : 1'bz;  // Controlled_Buffer controlled_buffer_8
endmodule

module _2seg (
  input  in_1,
  input  in_2,
  input  in_3,
  input  in_4,
  input  in_5,
  input  in_6,
  input  in_7,
  input  in_8,
  input  in_9,
  output out_10,
  output out_11,
  output out_12,
  output out_13,
  output out_14,
  output out_15,
  output out_16,
  output out_17,
  output out_18,
  output out_19,
  output out_20,
  output out_21,
  output out_22,
  output out_23
);

  wire c8_1_out_10, c8_1_out_11, c8_1_out_12, c8_1_out_13, c8_1_out_14, c8_1_out_15, c8_1_out_16, c8_1_out_17;

  C8 c8_1 (
    .in_2(in_1), .in_3(in_3), .in_4(in_4), .in_5(in_5), .in_6(in_6), .in_7(in_7), .in_8(in_8), .in_9(in_9),
    .out_10(c8_1_out_10), .out_11(c8_1_out_11), .out_12(c8_1_out_12), .out_13(c8_1_out_13),
    .out_14(c8_1_out_14), .out_15(c8_1_out_15), .out_16(c8_1_out_16), .out_17(c8_1_out_17), .in_1(in_2));
  Seg seg_1 (
    .in_1(c8_1_out_10), .in_2(c8_1_out_11), .in_3(c8_1_out_12), .in_4(c8_1_out_13), .out_5(out_10),
    .out_6(out_11), .out_7(out_12), .out_8(out_13), .out_9(out_14), .out_10(out_15), .out_11(out_16));
  Seg seg_2 (
    .in_1(c8_1_out_14), .in_2(c8_1_out_15), .in_3(c8_1_out_16), .in_4(c8_1_out_17), .out_5(out_17),
    .out_6(out_18), .out_7(out_19), .out_8(out_20), .out_9(out_21), .out_10(out_22), .out_11(out_23));
endmodule

module _16_4 (
  input  I0,
  input  I1,
  input  I2,
  input  I3,
  input  I4,
  input  I5,
  input  I6,
  input  I7,
  input  I8,
  input  I9,
  input  I10,
  input  I11,
  input  I12,
  input  I13,
  input  I14,
  input  I15,
  output O3,
  output O2,
  output O1,
  output O0
);

  or or_1 (O0, I1, I3, I5, I7, I9, I11, I13, I15);
  or or_2 (O1, I2, I3, I6, I7, I10, I11, I14, I15);
  or or_3 (O2, I4, I5, I6, I7, I12, I13, I14, I15);
  or or_4 (O3, I8, I9, I10, I11, I12, I13, I14, I15);
endmodule

module _16key (
  input  I0,
  input  I1,
  input  I2,
  input  I3,
  input  I4,
  input  I5,
  input  I6,
  input  I7,
  input  I8,
  input  I9,
  input  I10,
  input  I11,
  input  I12,
  input  in_14,
  input  I13,
  input  I14,
  input  I15,
  input  I0_2,
  input  I1_2,
  input  I2_2,
  input  I3_2,
  input  I4_2,
  input  I5_2,
  input  I6_2,
  input  I7_2,
  input  I8_2,
  input  I9_2,
  input  I10_2,
  input  I11_2,
  input  I12_2,
  input  I13_2,
  input  I14_2,
  input  I15_2,
  output out_34,
  output out_35,
  output out_36,
  output out_37,
  output out_38,
  output out_39,
  output out_40,
  output out_41
);

  wire n16_4_1_o0, n16_4_1_o1, n16_4_1_o2, n16_4_1_o3, n16_4_2_o0, n16_4_2_o1, n16_4_2_o2, n16_4_2_o3;

  _16_4 u_16_4_1 (
    .I0(I0), .I1(I1), .I2(I2), .I3(I3), .I4(I4), .I5(I5), .I6(I6), .I7(I7), .I8(I8), .I9(I9), .I10(I10),
    .I11(I11), .I12(I12), .I13(I13), .I14(I14), .I15(I15), .O3(n16_4_1_o3), .O2(n16_4_1_o2), .O1(n16_4_1_o1),
    .O0(n16_4_1_o0));
  _16_4 u_16_4_2 (
    .I0(I0_2), .I1(I1_2), .I2(I2_2), .I3(I3_2), .I4(I4_2), .I5(I5_2), .I6(I6_2), .I7(I7_2), .I8(I8_2),
    .I9(I9_2), .I10(I10_2), .I11(I11_2), .I12(I12_2), .I13(I13_2), .I14(I14_2), .I15(I15_2), .O3(n16_4_2_o3),
    .O2(n16_4_2_o2), .O1(n16_4_2_o1), .O0(n16_4_2_o0));
  C8 c8_1 (
    .in_2(n16_4_1_o3), .in_3(n16_4_1_o2), .in_4(n16_4_1_o1), .in_5(n16_4_1_o0), .in_6(n16_4_2_o3),
    .in_7(n16_4_2_o2), .in_8(n16_4_2_o1), .in_9(n16_4_2_o0), .out_10(out_34), .out_11(out_35),
    .out_12(out_36), .out_13(out_37), .out_14(out_38), .out_15(out_39), .out_16(out_40), .out_17(out_41),
    .in_1(in_14));
endmodule

module double_16key (
  input  I0,
  input  I1,
  input  I2,
  input  I3,
  input  I4,
  input  I5,
  input  I6,
  input  I7,
  input  I8,
  input  I9,
  input  I10,
  input  I11,
  input  in_13,
  input  in_14,
  input  I12,
  input  I13,
  input  I14,
  input  I15,
  input  I0_2,
  input  I1_2,
  input  I2_2,
  input  I3_2,
  input  I4_2,
  input  I5_2,
  input  I6_2,
  input  I7_2,
  input  I8_2,
  input  I9_2,
  input  I10_2,
  input  I11_2,
  input  I12_2,
  input  I13_2,
  input  I14_2,
  input  in_34,
  input  in_35,
  input  I15_2,
  output out_37,
  output out_38,
  output out_39,
  output out_40,
  output out_41,
  output out_42,
  output out_43,
  output out_44
);

  wire and_1_out, n16_4_1_o0, n16_4_1_o1, n16_4_1_o2, n16_4_1_o3, n16_4_2_o0, n16_4_2_o1, n16_4_2_o2,
       n16_4_2_o3, reg8_1_out_10, reg8_1_out_11, reg8_1_out_12, reg8_1_out_13, reg8_1_out_14, reg8_1_out_15,
       reg8_1_out_16, reg8_1_out_17;

  _16_4 u_16_4_1 (
    .I0(I0), .I1(I1), .I2(I2), .I3(I3), .I4(I4), .I5(I5), .I6(I6), .I7(I7), .I8(I8), .I9(I9), .I10(I10),
    .I11(I11), .I12(I12), .I13(I13), .I14(I14), .I15(I15), .O3(n16_4_1_o3), .O2(n16_4_1_o2), .O1(n16_4_1_o1),
    .O0(n16_4_1_o0));
  _16_4 u_16_4_2 (
    .I0(I0_2), .I1(I1_2), .I2(I2_2), .I3(I3_2), .I4(I4_2), .I5(I5_2), .I6(I6_2), .I7(I7_2), .I8(I8_2),
    .I9(I9_2), .I10(I10_2), .I11(I11_2), .I12(I12_2), .I13(I13_2), .I14(I14_2), .I15(I15_2), .O3(n16_4_2_o3),
    .O2(n16_4_2_o2), .O1(n16_4_2_o1), .O0(n16_4_2_o0));
  C8 c8_1 (
    .in_2(n16_4_1_o3), .in_3(n16_4_1_o2), .in_4(n16_4_1_o1), .in_5(n16_4_1_o0), .in_6(n16_4_2_o3),
    .in_7(n16_4_2_o2), .in_8(n16_4_2_o1), .in_9(n16_4_2_o0), .out_10(out_37), .out_11(out_38),
    .out_12(out_39), .out_13(out_40), .out_14(out_41), .out_15(out_42), .out_16(out_43), .out_17(out_44),
    .in_1(in_13));
  reg8 reg8_1 (
    .in_1(n16_4_1_o3), .in_2(n16_4_1_o2), .in_3(n16_4_1_o1), .in_4(n16_4_1_o0), .in_5(n16_4_2_o3),
    .in_6(n16_4_2_o2), .in_7(n16_4_2_o1), .in_9(n16_4_2_o0), .out_10(reg8_1_out_10), .out_11(reg8_1_out_11),
    .out_12(reg8_1_out_12), .out_13(reg8_1_out_13), .out_14(reg8_1_out_14), .out_15(reg8_1_out_15),
    .out_16(reg8_1_out_16), .out_17(reg8_1_out_17), .in_8(in_34));
  and and_1 (and_1_out, reg8_1_out_10, in_35);
  C8 c8_2 (
    .in_2(and_1_out), .in_3(reg8_1_out_11), .in_4(reg8_1_out_12), .in_5(reg8_1_out_13), .in_6(reg8_1_out_14),
    .in_7(reg8_1_out_15), .in_8(reg8_1_out_16), .in_9(reg8_1_out_17), .out_10(out_37), .out_11(out_38),
    .out_12(out_39), .out_13(out_40), .out_14(out_41), .out_15(out_42), .out_16(out_43), .out_17(out_44),
    .in_1(in_14));
endmodule

module reg8 (
  input  in_1,
  input  in_2,
  input  in_3,
  input  in_4,
  input  in_5,
  input  in_6,
  input  in_7,
  input  in_8,
  input  in_9,
  output out_10,
  output out_11,
  output out_12,
  output out_13,
  output out_14,
  output out_15,
  output out_16,
  output out_17
);

  Register register_1 (
    .D({in_1, in_2, in_3, in_4, in_5, in_6, in_7, in_9}),
    .Q({out_10, out_11, out_12, out_13, out_14, out_15, out_16, out_17}), .clk(in_8));  // open: en, clr
endmodule
