// Logisim project 数码管.circ as structural Verilog: 11 circuits, main circuit main
module main (
  input  in_1,
  input  in_2,
  input  in_3,
  input  in_4
);

  wire seg_1_out_5, seg_1_out_6, seg_1_out_7, seg_1_out_8, seg_1_out_9, seg_1_out_10, seg_1_out_11;

  Seg seg_1 (
    .in_1(in_1), .in_2(in_2), .in_3(in_3), .in_4(in_4), .out_5(seg_1_out_5), .out_6(seg_1_out_6),
    .out_7(seg_1_out_7), .out_8(seg_1_out_8), .out_9(seg_1_out_9), .out_10(seg_1_out_10),
    .out_11(seg_1_out_11));
  _7_Segment_Display #(.active("false")) u_7_segment_display_1 (
    .g(seg_1_out_11), .f(seg_1_out_10), .a(seg_1_out_5), .b(seg_1_out_6), .e(seg_1_out_9), .d(seg_1_out_8),
    .c(seg_1_out_7), .dp(1'b1));
endmodule

module Seg_A (
  input  D3,
  input  D2,
  input  D1,
  input  D0,
  output A
);

  wire not_1_out, not_2_out, not_3_out, not_4_out, x1_out, x2_out, x3_out, x4_out;

  not not_1 (not_1_out, D3);
  not not_2 (not_2_out, D2);
  not not_3 (not_3_out, D1);
  not not_4 (not_4_out, D0);
  and x1 (x1_out, not_1_out, not_2_out, not_3_out, D0);
  and x2 (x2_out, not_1_out, D2, not_3_out, not_4_out);
  and x3 (x3_out, D3, not_2_out, D1, D0);
  and x4 (x4_out, D3, D2, not_3_out, D0);
  or or_1 (A, x1_out, x2_out, x3_out, x4_out);
endmodule

module Seg_B (
  input  D3,
  input  D2,
  input  D1,
  input  D0,
  output B
);

  wire not_1_out, not_2_out, not_3_out, not_4_out, x1_out, x2_out, x3_out, x4_out, x5_out, x6_out;

  not not_1 (not_1_out, D3);
  not not_2 (not_2_out, D2);
  not not_3 (not_3_out, D1);
  not not_4 (not_4_out, D0);
  and x1 (x1_out, not_1_out, D2, not_3_out, D0);
  and x2 (x2_out, not_1_out, D2, D1, not_4_out);
  and x3 (x3_out, D3, not_2_out, D1, D0);
  and x4 (x4_out, D3, D2, not_3_out, not_4_out);
  and x5 (x5_out, D3, D2, D1, not_4_out);
  and x6 (x6_out, D3, D2, D1, D0);
  or or_1 (B, x1_out, x2_out, x3_out, x4_out, x5_out, x6_out);
endmodule

module Seg_C (
  input  D3,
  input  D2,
  input  D1,
  input  D0,
  output C
);

  wire not_1_out, not_2_out, not_3_out, not_4_out, x1_out, x2_out, x3_out, x4_out;

  not not_1 (not_1_out, D3);
  not not_2 (not_2_out, D2);
  not not_3 (not_3_out, D1);
  not not_4 (not_4_out, D0);
  and x1 (x1_out, not_1_out, not_2_out, D1, not_4_out);
  and x2 (x2_out, D3, D2, not_3_out, not_4_out);
  and x3 (x3_out, D3, D2, D1, not_4_out);
  and x4 (x4_out, D3, D2, D1, D0);
  or or_1 (C, x1_out, x2_out, x3_out, x4_out);
endmodule

module Seg_D (
  input  D3,
  input  D2,
  input  D1,
  input  D0,
  output D
);

  wire not_1_out, not_2_out, not_3_out, not_4_out, x1_out, x2_out, x3_out, x4_out, x5_out;

  not not_1 (not_1_out, D3);
  not not_2 (not_2_out, D2);
  not not_3 (not_3_out, D1);
  not not_4 (not_4_out, D0);
  and x1 (x1_out, not_1_out, not_2_out, not_3_out, D0);
  and x2 (x2_out, not_1_out, D2, not_3_out, not_4_out);
  and x3 (x3_out, not_1_out, D2, D1, D0);
  and x4 (x4_out, D3, not_2_out, D1, not_4_out);
  and x5 (x5_out, D3, D2, D1, D0);
  or or_1 (D, x1_out, x2_out, x3_out, x4_out, x5_out);
endmodule

module Seg_E (
  input  D3,
  input  D2,
  input  D1,
  input  D0,
  output E
);

  wire not_1_out, not_2_out, not_3_out, not_4_out, x1_out, x2_out, x3_out, x4_out, x5_out, x6_out;

  not not_1 (not_1_out, D3);
  not not_2 (not_2_out, D2);
  not not_3 (not_3_out, D1);
  not not_4 (not_4_out, D0);
  and x1 (x1_out, not_1_out, not_2_out, not_3_out, D0);
  and x2 (x2_out, not_1_out, not_2_out, D1, D0);
  and x3 (x3_out, not_1_out, D2, not_3_out, not_4_out);
  and x4 (x4_out, not_1_out, D2, not_3_out, D0);
  and x5 (x5_out, not_1_out, D2, D1, D0);
  and x6 (x6_out, D3, not_2_out, not_3_out, D0);
  or or_1 (E, x1_out, x2_out, x3_out, x4_out, x5_out, x6_out);
endmodule

module Seg_F (
  input  D3,
  input  D2,
  input  D1,
  input  D0,
  output F
);

  wire not_1_out, not_2_out, not_3_out, not_4_out, x1_out, x2_out, x3_out, x4_out, x5_out;

  not not_1 (not_1_out, D3);
  not not_2 (not_2_out, D2);
  not not_3 (not_3_out, D1);
  not not_4 (not_4_out, D0);
  and x1 (x1_out, not_1_out, not_2_out, not_3_out, D0);
  and x2 (x2_out, not_1_out, not_2_out, D1, not_4_out);
  and x3 (x3_out, not_1_out, not_2_out, D1, D0);
  and x4 (x4_out, not_1_out, D2, D1, D0);
  and x5 (x5_out, D3, D2, not_3_out, D0);
  or or_1 (F, x1_out, x2_out, x3_out, x4_out, x5_out);
endmodule

module Seg_G (
  input  D3,
  input  D2,
  input  D1,
  input  D0,
  output G
);

  wire not_1_out, not_2_out, not_3_out, not_4_out, x1_out, x2_out, x3_out, x4_out;

  not not_1 (not_1_out, D3);
  not not_2 (not_2_out, D2);
  not not_3 (not_3_out, D1);
  not not_4 (not_4_out, D0);
  and x1 (x1_out, not_1_out, not_2_out, not_3_out, not_4_out);
  and x2 (x2_out, not_1_out, not_2_out, not_3_out, D0);
  and x3 (x3_out, not_1_out, D2, D1, D0);
  and x4 (x4_out, D3, D2, not_3_out, not_4_out);
  or or_1 (G, x1_out, x2_out, x3_out, x4_out);
endmodule

module Seg (
  input  in_1,
  input  in_2,
  input  in_3,
  input  in_4,
  output out_5,
  output out_6,
  output out_7,
  output out_8,
  output out_9,
  output out_10,
  output out_11
);

  Seg_A seg_a_1 (.D3(in_1), .D2(in_2), .D1(in_3), .D0(in_4), .A(out_5));
  Seg_B seg_b_1 (.D3(in_1), .D2(in_2), .D1(in_3), .D0(in_4), .B(out_6));
  Seg_C seg_c_1 (.D3(in_1), .D2(in_2), .D1(in_3), .D0(in_4), .C(out_7));
  Seg_D seg_d_1 (.D3(in_1), .D2(in_2), .D1(in_3), .D0(in_4), .D(out_8));
  Seg_E seg_e_1 (.D3(in_1), .D2(in_2), .D1(in_3), .D0(in_4), .E(out_9));
  Seg_F seg_f_1 (.D3(in_1), .D2(in_2), .D1(in_3), .D0(in_4), .F(out_10));
  Seg_G seg_g_1 (.D3(in_1), .D2(in_2), .D1(in_3), .D0(in_4), .G(out_11));
endmodule

module _2Seg (
  input  in_1,
  input  in_2,
  input  in_3,
  input  in_4,
  input  in_5,
  input  in_6,
  input  in_7,
  input  in_8,
  input  in_9,
  output out_10,
  output out_11,
  output out_12,
  output out_13,
  output out_14,
  output out_15,
  output out_16,
  output out_17,
  output out_18,
  output out_19,
  output out_20,
  output out_21,
  output out_22,
  output out_23
);

  wire c8_1_out_10, c8_1_out_11, c8_1_out_12, c8_1_out_13, c8_1_out_14, c8_1_out_15, c8_1_out_16, c8_1_out_17;

  c8 c8_1 (
    .in_2(in_1), .in_3(in_3), .in_4(in_4), .in_5(in_5), .in_6(in_6), .in_7(in_7), .in_8(in_8), .in_9(in_9),
    .in_1(in_2), .out_10(c8_1_out_10), .out_11(c8_1_out_11), .out_12(c8_1_out_12), .out_13(c8_1_out_13),
    .out_14(c8_1_out_14), .out_15(c8_1_out_15), .out_16(c8_1_out_16), .out_17(c8_1_out_17));
  Seg seg_1 (
    .in_1(c8_1_out_10), .in_2(c8_1_out_11), .in_3(c8_1_out_12), .in_4(c8_1_out_13), .out_5(out_10),
    .out_6(out_11), .out_7(out_12), .out_8(out_13), .out_9(out_14), .out_10(out_15), .out_11(out_16));
  Seg seg_2 (
    .in_1(c8_1_out_14), .in_2(c8_1_out_15), .in_3(c8_1_out_16), .in_4(c8_1_out_17), .out_5(out_17),
    .out_6(out_18), .out_7(out_19), .out_8(out_20), .out_9(out_21), .out_10(out_22), .out_11(out_23));
endmodule

module c8 (
  input  in_1,
  input  in_2,
  input  in_3,
  input  in_4,
  input  in_5,
  input  in_6,
  input  in_7,
  input  in_8,
  input  in_9,
  output out_10,
  output out_11,
  output out_12,
  output out_13,
  output out_14,
  output out_15,
  output out_16,
  output out_17
);

  assign out_10 = in_1 ? in_2 : 1'bz;  // Controlled_Buffer controlled_buffer_1
  assign out_11 = in_1 ? in_3 : 1'bz;  // Controlled_Buffer controlled_buffer_2
  assign out_12 = in_1 ? in_4 : 1'bz;  // Controlled_Buffer controlled_buffer_3
  assign out_13 = in_1 ? in_5 : 1'bz;  // Controlled_Buffer controlled_buffer_4
  assign out_14 = in_1 ? in_6 : 1'bz;  // Controlled_Buffer controlled_buffer_5
  assign out_15 = in_1 ? in_7 : 1'bz;  // Controlled_Buffer controlled_buffer_6
  assign out_16 = in_1 ? in_8 : 1'bz;  // Controlled_Buffer controlled_buffer_7
  assign out_17 = in_1 ? in_9 : 1'bz;  // Controlled_Buffer controlled_buffer_8
endmodule
