// Logisim project 综合实验.circ as structural Verilog: 3 circuits, main circuit main
module main (
  input  I0,
  input  I1,
  input  I2,
  input  I3,
  input  I4,
  input  I5,
  input  I6,
  input  I7,
  input  I8,
  input  I9,
  input  I10,
  input  I11,
  input  I12,
  input  I13,
  input  I14,
  input  I15,
  input  I0_2,
  input  I1_2,
  input  I2_2,
  input  I3_2,
  input  I4_2,
  input  I5_2,
  input  I6_2,
  input  I7_2,
  input  I8_2,
  input  I9_2,
  input  I10_2,
  input  I11_2,
  input  I12_2,
  input  I13_2,
  input  I14_2,
  input  I15_2,
  input  W1,
  input  llen
);

  wire clock_1_out, n2seg_1_out_10, n2seg_1_out_11, n2seg_1_out_12, n2seg_1_out_13, n2seg_1_out_14,
       n2seg_1_out_15, n2seg_1_out_16, n2seg_1_out_17, n2seg_1_out_18, n2seg_1_out_19, n2seg_1_out_20,
       n2seg_1_out_21, n2seg_1_out_22, n2seg_1_out_23;
  wire [3:0] rom_1_data;
  wire [5:0] counter_1_q;
  wire [5:2] rom_1_data_2;
  wire [7:0] c_2_out_3, c_5_out_3, double_16key_1_out_44, main_1_result, \main_1_乘积低位 , r_1_out_3, r_2_out_3,
       r_3_out_3;
  wire [13:0] rom_2_data;

  double_16key double_16key_1 (
    .I0(I0), .I1(I1), .I2(I2), .I3(I3), .I4(I4), .I5(I5), .I6(I6), .I7(I7), .I8(I8), .I9(I9), .I10(I10),
    .I11(I11), .I12(I12), .I13(I13), .I14(I14), .I15(I15), .I0_2(I0_2), .I1_2(I1_2), .I2_2(I2_2),
    .I3_2(I3_2), .I4_2(I4_2), .I5_2(I5_2), .I6_2(I6_2), .I7_2(I7_2), .I8_2(I8_2), .I9_2(I9_2), .I10_2(I10_2),
    .I11_2(I11_2), .I12_2(I12_2), .I13_2(I13_2), .I14_2(I14_2), .I15_2(I15_2), .in_13(rom_2_data[9]),
    .in_14(rom_2_data[10]), .in_34(W1), .in_35(llen), .out_37(double_16key_1_out_44[7]),
    .out_38(double_16key_1_out_44[6]), .out_39(double_16key_1_out_44[5]), .out_40(double_16key_1_out_44[4]),
    .out_41(double_16key_1_out_44[3]), .out_42(double_16key_1_out_44[2]), .out_43(double_16key_1_out_44[1]),
    .out_44(double_16key_1_out_44[0]));
  LED led_1 (.in(double_16key_1_out_44[3]));
  LED \u_高  (.in(double_16key_1_out_44[7]));
  LED led_2 (.in(double_16key_1_out_44[2]));
  LED led_3 (.in(double_16key_1_out_44[6]));
  LED led_4 (.in(double_16key_1_out_44[1]));
  LED led_5 (.in(double_16key_1_out_44[5]));
  LED led_6 (.in(double_16key_1_out_44[4]));
  LED led_7 (.in(double_16key_1_out_44[0]));
  C c_1 (.in_2(r_2_out_3), .out_3(double_16key_1_out_44), .in_1(rom_2_data[7]));
  C c_2 (.in_2(double_16key_1_out_44), .out_3(c_2_out_3), .in_1(rom_2_data[8]));
  C c_3 (.in_2(main_1_result), .out_3(c_2_out_3), .in_1(rom_2_data[5]));
  C c_4 (.in_2(r_3_out_3), .out_3(double_16key_1_out_44), .in_1(rom_2_data[6]));
  ALU_main main_1 (
    .A(r_1_out_3), .B(r_3_out_3), .result(main_1_result), .\乘积低位 (\main_1_乘积低位 ), .OP(rom_1_data_2[4:2]),
    .LOAD(rom_2_data[2]), .in_5(rom_2_data[11]));
  R r_1 (.in_1(r_2_out_3), .out_3(r_1_out_3), .in_2(rom_2_data[2]));
  R r_2 (.in_1(c_2_out_3), .out_3(r_2_out_3), .in_2(rom_2_data[3]));
  C c_5 (.in_2(\main_1_乘积低位 ), .out_3(c_5_out_3), .in_1(rom_2_data[4]));
  R r_3 (.in_1(c_5_out_3), .out_3(r_3_out_3), .in_2(rom_2_data[1]));
  C c_6 (.in_2(r_2_out_3), .out_3(c_5_out_3), .in_1(rom_2_data[8]));
  _2Seg u_2seg_1 (
    .in_1(double_16key_1_out_44[7]), .in_3(double_16key_1_out_44[6]), .in_4(double_16key_1_out_44[5]),
    .in_5(double_16key_1_out_44[4]), .in_6(double_16key_1_out_44[3]), .in_7(double_16key_1_out_44[2]),
    .in_8(double_16key_1_out_44[1]), .in_9(double_16key_1_out_44[0]), .in_2(rom_2_data[0]),
    .out_10(n2seg_1_out_10), .out_11(n2seg_1_out_11), .out_12(n2seg_1_out_12), .out_13(n2seg_1_out_13),
    .out_14(n2seg_1_out_14), .out_15(n2seg_1_out_15), .out_16(n2seg_1_out_16), .out_17(n2seg_1_out_17),
    .out_18(n2seg_1_out_18), .out_19(n2seg_1_out_19), .out_20(n2seg_1_out_20), .out_21(n2seg_1_out_21),
    .out_22(n2seg_1_out_22), .out_23(n2seg_1_out_23));
  Counter #(.width(6), .max('h3f)) counter_1 (
    .Q(counter_1_q), .clk(clock_1_out), .clr(rom_2_data[12]));  // open: load, D, count, carry
  Clock clock_1 (.out(clock_1_out));
  _7_Segment_Display #(.active("false")) u_7_segment_display_1 (
    .g(n2seg_1_out_16), .f(n2seg_1_out_15), .a(n2seg_1_out_10), .b(n2seg_1_out_11), .e(n2seg_1_out_14),
    .d(n2seg_1_out_13), .c(n2seg_1_out_12), .dp(1'b1));
  _7_Segment_Display #(.active("false")) u_7_segment_display_2 (
    .g(n2seg_1_out_23), .f(n2seg_1_out_22), .a(n2seg_1_out_17), .b(n2seg_1_out_18), .e(n2seg_1_out_21),
    .d(n2seg_1_out_20), .c(n2seg_1_out_19), .dp(1'b1));
  ROM #(.addrWidth(4)) rom_1 (.addr(counter_1_q[5:2]), .data({rom_1_data_2, rom_1_data}));  // open: sel
  ROM #(.addrWidth(6), .dataWidth(14)) rom_2 (.addr({rom_1_data_2, counter_1_q[1:0]}), .data(rom_2_data));  // open: sel

  // Notes on the sheet:
  //   contents of rom_1 (hex, n*v repeats v):
  //   a1 e1 b1 50 c1 0 0 91
  //   contents of rom_2 (hex, n*v repeats v):
  //   1 801 1 801 16*0 5 21 29 21 6*0 5 805 8*0 501 509 501 501 301 309 301 0 81 81 81 0 41 41 41 0 503
  //   501 1 0 0 31 3b 31
endmodule

module C (
  input  in_1,
  input  [7:0] in_2,
  output [7:0] out_3
);

  assign out_3[0] = in_1 ? in_2[0] : 1'bz;  // Controlled_Buffer controlled_buffer_1
  assign out_3[1] = in_1 ? in_2[1] : 1'bz;  // Controlled_Buffer controlled_buffer_2
  assign out_3[2] = in_1 ? in_2[2] : 1'bz;  // Controlled_Buffer controlled_buffer_3
  assign out_3[3] = in_1 ? in_2[3] : 1'bz;  // Controlled_Buffer controlled_buffer_4
  assign out_3[4] = in_1 ? in_2[4] : 1'bz;  // Controlled_Buffer controlled_buffer_5
  assign out_3[5] = in_1 ? in_2[5] : 1'bz;  // Controlled_Buffer controlled_buffer_6
  assign out_3[6] = in_1 ? in_2[6] : 1'bz;  // Controlled_Buffer controlled_buffer_7
  assign out_3[7] = in_1 ? in_2[7] : 1'bz;  // Controlled_Buffer controlled_buffer_8
endmodule

module R (
  input  [7:0] in_1,
  input  in_2,
  output [7:0] out_3
);

  Register register_1 (.D(in_1), .Q(out_3), .clk(in_2));  // open: en, clr
endmodule
