// Logisim project 自动执行逻辑+控制器设计.circ as structural Verilog
module HA (
  input  A,
  input  B,
  output S,
  output C
);

  wire and_2_out, and_3_out, not_1_out, not_2_out;

  not not_1 (not_1_out, A);
  not not_2 (not_2_out, B);
  and and_1 (C, A, B);
  and and_2 (and_2_out, not_1_out, B);
  and and_3 (and_3_out, A, not_2_out);
  or or_1 (S, and_2_out, and_3_out);
endmodule

module FA (
  input  Cin,
  input  B,
  input  A,
  output Sum,
  output Cout
);

  wire ha_1_c, ha_1_s, ha_2_c;

  HA ha_1 (.A(B), .B(A), .S(ha_1_s), .C(ha_1_c));
  HA ha_2 (.A(Cin), .B(ha_1_s), .S(Sum), .C(ha_2_c));
  or or_1 (Cout, ha_2_c, ha_1_c);
endmodule

module _8adder (
  input  B7,
  input  B6,
  input  B5,
  input  B4,
  input  B3,
  input  B2,
  input  B1,
  input  B0,
  input  A7,
  input  A6,
  input  A5,
  input  A4,
  input  A3,
  input  A2,
  input  A1,
  input  A0,
  output C,
  output S7,
  output S6,
  output S5,
  output S4,
  output S3,
  output S2,
  output S1,
  output S0
);

  wire fa_1_cout, fa_2_cout, fa_3_cout, fa_4_cout, fa_5_cout, fa_6_cout, fa_7_cout;

  FA fa_1 (.Cin(1'b0), .B(B0), .A(A0), .Sum(S0), .Cout(fa_1_cout));
  FA fa_2 (.Cin(fa_3_cout), .B(B2), .A(A2), .Sum(S2), .Cout(fa_2_cout));
  FA fa_3 (.Cin(fa_1_cout), .B(B1), .A(A1), .Sum(S1), .Cout(fa_3_cout));
  FA fa_4 (.Cin(fa_2_cout), .B(B3), .A(A3), .Sum(S3), .Cout(fa_4_cout));
  FA fa_5 (.Cin(fa_6_cout), .B(B5), .A(A5), .Sum(S5), .Cout(fa_5_cout));
  FA fa_6 (.Cin(fa_4_cout), .B(B4), .A(A4), .Sum(S4), .Cout(fa_6_cout));
  FA fa_7 (.Cin(fa_5_cout), .B(B6), .A(A6), .Sum(S6), .Cout(fa_7_cout));
  FA fa_8 (.Cin(fa_7_cout), .B(B7), .A(A7), .Sum(S7), .Cout(C));
endmodule

module ALU (
  input  I0,
  input  I1,
  input  I2,
  input  I3,
  input  I4,
  input  I5,
  input  I6,
  input  I7,
  input  I8,
  input  I9,
  input  I10,
  input  I11,
  input  I12,
  input  I13,
  input  I14,
  input  I15,
  input  I0_2,
  input  I1_2,
  input  I2_2,
  input  I3_2,
  input  I4_2,
  input  I5_2,
  input  I6_2,
  input  I7_2,
  input  I8_2,
  input  I9_2,
  input  I10_2,
  input  I11_2,
  input  I12_2,
  input  I13_2,
  input  I14_2,
  input  I15_2,
  input  W1,
  input  llen,
  output out_35
);

  wire c8_1_out_10, c8_1_out_11, c8_1_out_12, c8_1_out_13, c8_1_out_14, c8_1_out_15, c8_1_out_16,
       c8_1_out_17, clock_1_out, double_16key_1_out_37, double_16key_1_out_38, double_16key_1_out_39,
       double_16key_1_out_40, double_16key_1_out_41, double_16key_1_out_42, double_16key_1_out_43,
       double_16key_1_out_44, n2seg_1_out_10, n2seg_1_out_11, n2seg_1_out_12, n2seg_1_out_13, n2seg_1_out_14,
       n2seg_1_out_15, n2seg_1_out_16, n2seg_1_out_17, n2seg_1_out_18, n2seg_1_out_19, n2seg_1_out_20,
       n2seg_1_out_21, n2seg_1_out_22, n2seg_1_out_23, n8adder_1_s0, n8adder_1_s1, n8adder_1_s2,
       n8adder_1_s3, n8adder_1_s4, n8adder_1_s5, n8adder_1_s6, n8adder_1_s7, reg8_1_out_10, reg8_1_out_11,
       reg8_1_out_12, reg8_1_out_13, reg8_1_out_14, reg8_1_out_15, reg8_1_out_16, reg8_1_out_17,
       reg8_2_out_10, reg8_2_out_11, reg8_2_out_12, reg8_2_out_13, reg8_2_out_14, reg8_2_out_15,
       reg8_2_out_16, reg8_2_out_17, reg8_3_out_10, reg8_3_out_11, reg8_3_out_12, reg8_3_out_13,
       reg8_3_out_14, reg8_3_out_15, reg8_3_out_16, reg8_3_out_17;
  wire [4:2] rom_1_data;
  wire [5:0] counter_1_q;
  wire [6:3] rom_1_data_2;
  wire [10:0] rom_2_data;

  double_16key double_16key_1 (
    .I0(I0), .I1(I1), .I2(I2), .I3(I3), .I4(I4), .I5(I5), .I6(I6), .I7(I7), .I8(I8), .I9(I9), .I10(I10),
    .I11(I11), .I12(I12), .I13(I13), .I14(I14), .I15(I15), .I0_2(I0_2), .I1_2(I1_2), .I2_2(I2_2),
    .I3_2(I3_2), .I4_2(I4_2), .I5_2(I5_2), .I6_2(I6_2), .I7_2(I7_2), .I8_2(I8_2), .I9_2(I9_2), .I10_2(I10_2),
    .I11_2(I11_2), .I12_2(I12_2), .I13_2(I13_2), .I14_2(I14_2), .I15_2(I15_2), .in_13(rom_2_data[8]),
    .in_14(rom_2_data[7]), .in_34(W1), .in_35(llen), .out_37(double_16key_1_out_37),
    .out_38(double_16key_1_out_38), .out_39(double_16key_1_out_39), .out_40(double_16key_1_out_40),
    .out_41(double_16key_1_out_41), .out_42(double_16key_1_out_42), .out_43(double_16key_1_out_43),
    .out_44(double_16key_1_out_44));
  LED led_1 (.in(double_16key_1_out_37));
  LED led_2 (.in(double_16key_1_out_41));
  LED led_3 (.in(double_16key_1_out_42));
  LED led_4 (.in(double_16key_1_out_38));
  LED led_5 (.in(double_16key_1_out_39));
  LED led_6 (.in(double_16key_1_out_40));
  LED led_7 (.in(double_16key_1_out_43));
  LED led_8 (.in(double_16key_1_out_44));
  C8 c8_1 (
    .in_2(double_16key_1_out_44), .in_3(double_16key_1_out_43), .in_4(double_16key_1_out_42),
    .in_5(double_16key_1_out_41), .in_6(double_16key_1_out_40), .in_7(double_16key_1_out_39),
    .in_8(double_16key_1_out_38), .in_9(double_16key_1_out_37), .out_10(c8_1_out_10), .out_11(c8_1_out_11),
    .out_12(c8_1_out_12), .out_13(c8_1_out_13), .out_14(c8_1_out_14), .out_15(c8_1_out_15),
    .out_16(c8_1_out_16), .out_17(c8_1_out_17), .in_1(rom_2_data[6]));
  C8 c8_2 (
    .in_2(n8adder_1_s0), .in_3(n8adder_1_s1), .in_4(n8adder_1_s2), .in_5(n8adder_1_s3), .in_6(n8adder_1_s4),
    .in_7(n8adder_1_s5), .in_8(n8adder_1_s6), .in_9(n8adder_1_s7), .out_10(c8_1_out_17),
    .out_11(c8_1_out_16), .out_12(c8_1_out_15), .out_13(c8_1_out_14), .out_14(c8_1_out_13),
    .out_15(c8_1_out_12), .out_16(c8_1_out_11), .out_17(c8_1_out_10), .in_1(rom_2_data[4]));
  C8 c8_3 (
    .in_2(reg8_2_out_17), .in_3(reg8_2_out_16), .in_4(reg8_2_out_15), .in_5(reg8_2_out_14),
    .in_6(reg8_2_out_13), .in_7(reg8_2_out_12), .in_8(reg8_2_out_11), .in_9(reg8_2_out_10),
    .out_10(double_16key_1_out_37), .out_11(double_16key_1_out_38), .out_12(double_16key_1_out_39),
    .out_13(double_16key_1_out_40), .out_14(double_16key_1_out_41), .out_15(double_16key_1_out_42),
    .out_16(double_16key_1_out_43), .out_17(double_16key_1_out_44), .in_1(rom_2_data[5]));
  _8adder u_8adder_1 (
    .B7(reg8_1_out_10), .B6(reg8_1_out_11), .B5(reg8_1_out_12), .B4(reg8_1_out_13), .B3(reg8_1_out_14),
    .B2(reg8_1_out_15), .B1(reg8_1_out_16), .B0(reg8_1_out_17), .A7(reg8_3_out_10), .A6(reg8_3_out_11),
    .A5(reg8_3_out_12), .A4(reg8_3_out_13), .A3(reg8_3_out_14), .A2(reg8_3_out_15), .A1(reg8_3_out_16),
    .A0(reg8_3_out_17), .C(out_35), .S7(n8adder_1_s7), .S6(n8adder_1_s6), .S5(n8adder_1_s5),
    .S4(n8adder_1_s4), .S3(n8adder_1_s3), .S2(n8adder_1_s2), .S1(n8adder_1_s1), .S0(n8adder_1_s0));
  reg8 reg8_1 (
    .in_1(reg8_2_out_10), .in_2(reg8_2_out_11), .in_3(reg8_2_out_12), .in_4(reg8_2_out_13),
    .in_5(reg8_2_out_14), .in_6(reg8_2_out_15), .in_7(reg8_2_out_16), .in_9(reg8_2_out_17),
    .out_10(reg8_1_out_10), .out_11(reg8_1_out_11), .out_12(reg8_1_out_12), .out_13(reg8_1_out_13),
    .out_14(reg8_1_out_14), .out_15(reg8_1_out_15), .out_16(reg8_1_out_16), .out_17(reg8_1_out_17),
    .in_8(rom_2_data[2]));
  reg8 reg8_2 (
    .in_1(c8_1_out_17), .in_2(c8_1_out_16), .in_3(c8_1_out_15), .in_4(c8_1_out_14), .in_5(c8_1_out_13),
    .in_6(c8_1_out_12), .in_7(c8_1_out_11), .in_9(c8_1_out_10), .out_10(reg8_2_out_10),
    .out_11(reg8_2_out_11), .out_12(reg8_2_out_12), .out_13(reg8_2_out_13), .out_14(reg8_2_out_14),
    .out_15(reg8_2_out_15), .out_16(reg8_2_out_16), .out_17(reg8_2_out_17), .in_8(rom_2_data[3]));
  reg8 reg8_3 (
    .in_1(reg8_2_out_10), .in_2(reg8_2_out_11), .in_3(reg8_2_out_12), .in_4(reg8_2_out_13),
    .in_5(reg8_2_out_14), .in_6(reg8_2_out_15), .in_7(reg8_2_out_16), .in_9(reg8_2_out_17),
    .out_10(reg8_3_out_10), .out_11(reg8_3_out_11), .out_12(reg8_3_out_12), .out_13(reg8_3_out_13),
    .out_14(reg8_3_out_14), .out_15(reg8_3_out_15), .out_16(reg8_3_out_16), .out_17(reg8_3_out_17),
    .in_8(rom_2_data[1]));
  Clock clock_1 (.out(clock_1_out));
  _2seg u_2seg_1 (
    .in_1(double_16key_1_out_37), .in_3(double_16key_1_out_38), .in_4(double_16key_1_out_39),
    .in_5(double_16key_1_out_40), .in_6(double_16key_1_out_41), .in_7(double_16key_1_out_42),
    .in_8(double_16key_1_out_43), .in_9(double_16key_1_out_44), .in_2(rom_2_data[0]),
    .out_10(n2seg_1_out_10), .out_11(n2seg_1_out_11), .out_12(n2seg_1_out_12), .out_13(n2seg_1_out_13),
    .out_14(n2seg_1_out_14), .out_15(n2seg_1_out_15), .out_16(n2seg_1_out_16), .out_17(n2seg_1_out_17),
    .out_18(n2seg_1_out_18), .out_19(n2seg_1_out_19), .out_20(n2seg_1_out_20), .out_21(n2seg_1_out_21),
    .out_22(n2seg_1_out_22), .out_23(n2seg_1_out_23));
  Counter #(.width(6), .max('h3f)) counter_1 (
    .Q(counter_1_q), .clk(clock_1_out), .clr(rom_2_data[9]));  // open: load, D, count, carry
  _7_Segment_Display #(.active("false")) u_7_segment_display_1 (
    .g(n2seg_1_out_16), .f(n2seg_1_out_15), .a(n2seg_1_out_10), .b(n2seg_1_out_11), .e(n2seg_1_out_14),
    .d(n2seg_1_out_13), .c(n2seg_1_out_12), .dp(1'b1));
  _7_Segment_Display #(.active("false")) u_7_segment_display_2 (
    .g(n2seg_1_out_23), .f(n2seg_1_out_22), .a(n2seg_1_out_17), .b(n2seg_1_out_18), .e(n2seg_1_out_21),
    .d(n2seg_1_out_20), .c(n2seg_1_out_19), .dp(1'b1));
  ROM #(.addrWidth(4), .dataWidth(7)) rom_1 (.addr(counter_1_q[5:2]), .data({rom_1_data_2, rom_1_data}));  // open: sel
  ROM #(.addrWidth(5), .dataWidth(11)) rom_2 (.addr({rom_1_data, counter_1_q[1:0]}), .data(rom_2_data));  // open: sel

  // Notes on the sheet:
  //   contents of rom_1 (hex, n*v repeats v):
  //   14 7 15 2 16 4*0 1
  //   contents of rom_2 (hex, n*v repeats v):
  //   4*0 200 0 0 0 5 11 19 11 405 411 419 411 141 149 141 0 81 c1 c9 c1 21 0 0 0 3 1
endmodule
